// Logisim project main.circ as structural Verilog: 24 circuits, main circuit main
module main (
);

  wire and_1_out, and_2_out, button_2_out, button_3_out, clk, cmd_show, counter_1_carry, drawing, not_1_out,
       not_2_out, or_1_out, pull_resistor_1_node, register_1_q, shot, transistor_1_out;
  wire [2:0] multiplexer_1_out, multiplexer_2_out, x_vec;
  wire [3:0] bit_extender_2_out, bit_extender_3_out, bit_extender_4_out;
  wire [4:0] counter_1_q, simple_drawer_32x32_1_cur_line, \схема_расчётов_1_x , \схема_расчётов_1_y ;
  wire [15:0] adder_1_out, bit_extender_1_out, divider_1_out, divider_1_rem, divider_2_rem, hp,
       multiplier_1_out, score, \схема_расчётов_1_command , \схема_расчётов_1_id ;
  wire [31:0] rom_1_data, simple_drawer_32x32_1_line_x1, video_buffer_32x32_1_out_5,
       video_buffer_32x32_1_out_6, video_buffer_32x32_1_out_7, video_buffer_32x32_1_out_8,
       video_buffer_32x32_1_out_9, video_buffer_32x32_1_out_10, video_buffer_32x32_1_out_11,
       video_buffer_32x32_1_out_12, video_buffer_32x32_1_out_13, video_buffer_32x32_1_out_14,
       video_buffer_32x32_1_out_15, video_buffer_32x32_1_out_16, video_buffer_32x32_1_out_17,
       video_buffer_32x32_1_out_18, video_buffer_32x32_1_out_19, video_buffer_32x32_1_out_20,
       video_buffer_32x32_1_out_21, video_buffer_32x32_1_out_22, video_buffer_32x32_1_out_23,
       video_buffer_32x32_1_out_24, video_buffer_32x32_1_out_25, video_buffer_32x32_1_out_26,
       video_buffer_32x32_1_out_27, video_buffer_32x32_1_out_28, video_buffer_32x32_1_out_29,
       video_buffer_32x32_1_out_30, video_buffer_32x32_1_out_31, video_buffer_32x32_1_out_32,
       video_buffer_32x32_1_out_33, video_buffer_32x32_1_out_34, video_buffer_32x32_1_out_35,
       video_buffer_32x32_1_out_36;

  Clock clock_1 (.out(clk));
  simple_drawer_32x32 simple_drawer_32x32_1 (
    .x(\схема_расчётов_1_x ), .y(\схема_расчётов_1_y ), .texture_line(counter_1_q),
    .texture_input(rom_1_data), .cur_line(simple_drawer_32x32_1_cur_line),
    .line_x1(simple_drawer_32x32_1_line_x1));
  Transistor #(.\type ("n"), .gate("br")) transistor_1 (.in(clk), .out(transistor_1_out), .gate(drawing));
  Counter #(.width(5), .max('h2)) counter_1 (
    .Q(counter_1_q), .carry(counter_1_carry), .clk(transistor_1_out), .clr(and_1_out));  // open: load, D, count
  and and_1 (and_1_out, ~clk, counter_1_carry);  // AND_Gate
  Register #(.width(1)) register_1 (
    .D(pull_resistor_1_node), .Q(register_1_q), .clk(pull_resistor_1_node), .clr(and_1_out));  // open: en
  not not_1 (not_1_out, clk);
  Register #(.width(1)) register_2 (.D(register_1_q), .Q(drawing), .clk(not_1_out), .clr(and_1_out));  // open: en
  or or_1 (or_1_out, drawing, register_1_q, and_1_out);
  assign bit_extender_1_out = {{11{1'b0}}, counter_1_q};  // Bit_Extender bit_extender_1
  \Схема_расчётов  \u_схема_расчётов_1  (
    .player_inp_x(x_vec), .player_inp_y(3'b100), .ID(\схема_расчётов_1_id ), .X(\схема_расчётов_1_x ),
    .Y(\схема_расчётов_1_y ), .Command(\схема_расчётов_1_command ), .clock(clk), .drawing(or_1_out),
    .score(score), .shot(shot), .hp(hp));
  // Probe on \схема_расчётов_1_id 
  Multiplier #(.width(16)) multiplier_1 (
    .a(\схема_расчётов_1_id ), .b(16'h3), .out(multiplier_1_out));  // open: cin, cout
  Pull_Resistor pull_resistor_1 (.node(pull_resistor_1_node));
  Comparator #(.width(16), .mode("unsigned")) comparator_1 (
    .a(\схема_расчётов_1_command ), .b(16'h1), .eq(pull_resistor_1_node));  // open: gt, lt
  Comparator #(.width(16), .mode("unsigned")) comparator_2 (
    .a(\схема_расчётов_1_command ), .b(16'h2), .eq(cmd_show));  // open: gt, lt
  Adder #(.width(16)) adder_1 (.a(bit_extender_1_out), .b(multiplier_1_out), .out(adder_1_out));  // open: cin, cout
  ROM #(.addrWidth(16), .dataWidth(32)) rom_1 (.addr(adder_1_out), .data(rom_1_data));  // open: sel
  DotMatrix #(.inputtype("row"), .matrixcols(32), .matrixrows(32)) dotmatrix_1 (
    .row0(video_buffer_32x32_1_out_5), .row1(video_buffer_32x32_1_out_6), .row2(video_buffer_32x32_1_out_7),
    .row3(video_buffer_32x32_1_out_8), .row4(video_buffer_32x32_1_out_9), .row5(video_buffer_32x32_1_out_10),
    .row6(video_buffer_32x32_1_out_11), .row7(video_buffer_32x32_1_out_12),
    .row8(video_buffer_32x32_1_out_13), .row9(video_buffer_32x32_1_out_14),
    .row10(video_buffer_32x32_1_out_15), .row11(video_buffer_32x32_1_out_16),
    .row12(video_buffer_32x32_1_out_17), .row13(video_buffer_32x32_1_out_18),
    .row14(video_buffer_32x32_1_out_19), .row15(video_buffer_32x32_1_out_20),
    .row16(video_buffer_32x32_1_out_21), .row17(video_buffer_32x32_1_out_22),
    .row18(video_buffer_32x32_1_out_23), .row19(video_buffer_32x32_1_out_24),
    .row20(video_buffer_32x32_1_out_25), .row21(video_buffer_32x32_1_out_26),
    .row22(video_buffer_32x32_1_out_27), .row23(video_buffer_32x32_1_out_28),
    .row24(video_buffer_32x32_1_out_29), .row25(video_buffer_32x32_1_out_30),
    .row26(video_buffer_32x32_1_out_31), .row27(video_buffer_32x32_1_out_32),
    .row28(video_buffer_32x32_1_out_33), .row29(video_buffer_32x32_1_out_34),
    .row30(video_buffer_32x32_1_out_35), .row31(video_buffer_32x32_1_out_36));
  video_buffer_32x32 video_buffer_32x32_1 (
    .in_1(simple_drawer_32x32_1_line_x1), .write(and_2_out), .y(simple_drawer_32x32_1_cur_line),
    .show(cmd_show), .out_5(video_buffer_32x32_1_out_5), .out_6(video_buffer_32x32_1_out_6),
    .out_7(video_buffer_32x32_1_out_7), .out_8(video_buffer_32x32_1_out_8),
    .out_9(video_buffer_32x32_1_out_9), .out_10(video_buffer_32x32_1_out_10),
    .out_11(video_buffer_32x32_1_out_11), .out_12(video_buffer_32x32_1_out_12),
    .out_13(video_buffer_32x32_1_out_13), .out_14(video_buffer_32x32_1_out_14),
    .out_15(video_buffer_32x32_1_out_15), .out_16(video_buffer_32x32_1_out_16),
    .out_17(video_buffer_32x32_1_out_17), .out_18(video_buffer_32x32_1_out_18),
    .out_19(video_buffer_32x32_1_out_19), .out_20(video_buffer_32x32_1_out_20),
    .out_21(video_buffer_32x32_1_out_21), .out_22(video_buffer_32x32_1_out_22),
    .out_23(video_buffer_32x32_1_out_23), .out_24(video_buffer_32x32_1_out_24),
    .out_25(video_buffer_32x32_1_out_25), .out_26(video_buffer_32x32_1_out_26),
    .out_27(video_buffer_32x32_1_out_27), .out_28(video_buffer_32x32_1_out_28),
    .out_29(video_buffer_32x32_1_out_29), .out_30(video_buffer_32x32_1_out_30),
    .out_31(video_buffer_32x32_1_out_31), .out_32(video_buffer_32x32_1_out_32),
    .out_33(video_buffer_32x32_1_out_33), .out_34(video_buffer_32x32_1_out_34),
    .out_35(video_buffer_32x32_1_out_35), .out_36(video_buffer_32x32_1_out_36));
  and and_2 (and_2_out, drawing, not_2_out);
  not not_2 (not_2_out, clk);
  Button button_1 (.out(shot));
  Multiplexer #(.width(3), .enable("false")) multiplexer_1 (
    .in0(3'b100), .in1(3'b010), .out(multiplexer_1_out), .sel(button_3_out));
  Button button_2 (.out(button_2_out));
  Button button_3 (.out(button_3_out));
  Transistor #(.width(3)) transistor_2 (.in(multiplexer_1_out), .out(x_vec), .gate(button_2_out));
  Transistor #(.width(3)) transistor_3 (.in(multiplexer_2_out), .out(x_vec), .gate(button_3_out));
  Multiplexer #(.width(3), .enable("false")) multiplexer_2 (
    .in0(3'b100), .in1(3'b110), .out(multiplexer_2_out), .sel(button_2_out));
  Hex_Digit_Display hex_digit_display_1 (.value(bit_extender_2_out));  // open: dp
  Bit_Extender #(.in_width(16), .out_width(4)) bit_extender_2 (.in(hp), .out(bit_extender_2_out));
  Hex_Digit_Display hex_digit_display_2 (.value(bit_extender_3_out));  // open: dp
  Hex_Digit_Display hex_digit_display_3 (.value(bit_extender_4_out));  // open: dp
  Divider #(.width(16)) divider_1 (.a(score), .b(16'ha), .out(divider_1_out), .rem(divider_1_rem));  // open: upper
  Divider #(.width(16)) divider_2 (.a(divider_1_out), .b(16'ha), .rem(divider_2_rem));  // open: out, upper
  Bit_Extender #(.in_width(16), .out_width(4)) bit_extender_3 (.in(divider_2_rem), .out(bit_extender_3_out));
  Bit_Extender #(.in_width(16), .out_width(4)) bit_extender_4 (.in(divider_1_rem), .out(bit_extender_4_out));

  // Notes on the sheet:
  //   texture line counter
  //   contents of rom_1 (hex, n*v repeats v):
  //   2 7 5 2 5 5 0 0 0 2 7 5 2 5 5 7 5 5 2 7 7 2 5 7 2 5 5 0 0 0 1 1 1 1151 1351 1551 1955 1155 114a
  //   7ce381 41441 3ce441 50441 51441 7ce39f 1 1 1 0 0 0 2 1 0 2 3 0 3 3
  //   Shoot
  //   <-
  //   Movement
  //   ->
  //   HP
  //   SCORE
endmodule

module CDM16 (
  input  [15:0] adr,
  input  [15:0] val,
  input  clock,
  input  write,
  input  hold,
  input  end_cycle,
  output drawing,
  output [15:0] id,
  output [15:0] x,
  output [15:0] y,
  output [15:0] command,
  output collide,
  output wait_int__checker,
  output run,
  output [15:0] score,
  output button,
  output gg,
  output win,
  output [15:0] hp
);

  wire and_2_out, and_3_out, and_4_out, and_5_out, and_6_out, and_7_out, and_8_out, and_9_out, and_10_out,
       and_11_out, and_12_out, and_13_out, and_14_out, and_15_out, and_16_out, bit_extender_1_out,
       cdm_16_1_p3, cdm_16_1_p4, code, comparator_1_eq, comparator_3_eq, comparator_5_eq, comparator_9_eq,
       comparator_13_eq, comparator_15_eq, d_ff_1_q, data, decoder_1_out0, decoder_1_out1, initialized, mem,
       not_1_out, not_2_out, not_3_out, not_4_out, not_5_out, not_8_out, or_1_out, or_2_out,
       pull_resistor_6_node, pull_resistor_8_node, pull_resistor_10_node, pull_resistor_11_node,
       pull_resistor_12_node, pull_resistor_14_node, pull_resistor_15_node, pull_resistor_16_node,
       pull_resistor_17_node, read_write, transistor_3_out, transistor_6_out, word, write_t;
  wire [15:0] cdm_16_1_p8, cdm_16_1_p9, cdm_16_1_p10, controlled_buffer_2_out, register_1_q, register_2_q,
       register_3_q, register_4_q, register_5_q, register_6_q, register_7_q, register_9_q, register_10_q,
       register_11_q, transistor_4_out;

  // Debugger debugger_1: pin names not known
  and and_1 (write_t, write, d_ff_1_q);
  not not_1 (not_1_out, clock);
  D_Flip_Flop d_ff_1 (.clk(not_1_out), .D(or_1_out), .Q(d_ff_1_q));  // open: Qn, preset, en, reset
  or or_1 (or_1_out, write, and_2_out, or_2_out);
  buf or_2 (or_2_out, hold);  // OR_Gate
  and and_2 (and_2_out, ~initialized, wait_int__checker);  // AND_Gate
  // CdM_16 cdm_16_1: pin names not known; wires that end beside it: d_ff_1_q, clock, cdm_16_1_p3, cdm_16_1_p4, mem, read_write, word, cdm_16_1_p8, cdm_16_1_p9, cdm_16_1_p10
  // Probe on cdm_16_1_p3
  not not_2 (not_2_out, write_t);
  not not_3 (not_3_out, write_t);
  assign cdm_16_1_p10 = and_4_out ? controlled_buffer_2_out : 16'bz;  // Controlled_Buffer controlled_buffer_1
  assign controlled_buffer_2_out = and_3_out ? cdm_16_1_p9 : 16'bz;  // Controlled_Buffer controlled_buffer_2
  and and_3 (and_3_out, not_2_out, not_4_out);
  not not_4 (not_4_out, read_write);
  not not_5 (not_5_out, read_write);
  and and_4 (and_4_out, not_3_out, read_write);
  Transistor transistor_1 (.in(decoder_1_out0), .out(code), .gate(write_t));
  Pull_Resistor pull_resistor_1 (.node(code));
  Transistor #(.gate("br")) transistor_2 (.in(decoder_1_out1), .out(data), .gate(write_t));
  Pull_Resistor #(.pull(1)) pull_resistor_2 (.node(data));
  Decoder #(.disabled(0)) decoder_1 (.out0(decoder_1_out0), .out1(decoder_1_out1), .sel(cdm_16_1_p4), .en(mem));
  Transistor transistor_3 (.in(not_5_out), .out(transistor_3_out), .gate(write_t));
  Pull_Resistor #(.pull(1)) pull_resistor_3 (.node(transistor_3_out));
  Transistor #(.\type ("n"), .width(16)) transistor_4 (.in(adr), .out(transistor_4_out), .gate(write_t));
  Transistor #(.gate("br"), .width(16)) transistor_5 (.in(cdm_16_1_p8), .out(transistor_4_out), .gate(write_t));
  // Probe on transistor_4_out
  Transistor transistor_6 (.in(word), .out(transistor_6_out), .gate(write_t));
  Pull_Resistor #(.pull(1)) pull_resistor_4 (.node(transistor_6_out));
  Comparator #(.width(16)) comparator_1 (.a(transistor_4_out), .b(16'h86), .eq(comparator_1_eq));  // open: gt, lt
  Pull_Resistor pull_resistor_5 (.node(comparator_1_eq));
  Pull_Resistor pull_resistor_6 (.node(pull_resistor_6_node));
  Comparator #(.width(16)) comparator_2 (.a(transistor_4_out), .b(16'h88), .eq(pull_resistor_6_node));  // open: gt, lt
  Comparator #(.width(16)) comparator_3 (.a(transistor_4_out), .b(16'h8a), .eq(comparator_3_eq));  // open: gt, lt
  Pull_Resistor pull_resistor_7 (.node(comparator_3_eq));
  Pull_Resistor pull_resistor_8 (.node(pull_resistor_8_node));
  Comparator #(.width(16)) comparator_4 (.a(transistor_4_out), .b(16'h8c), .eq(pull_resistor_8_node));  // open: gt, lt
  Comparator #(.width(16)) comparator_5 (.a(transistor_4_out), .b(16'h94), .eq(comparator_5_eq));  // open: gt, lt
  Pull_Resistor pull_resistor_9 (.node(comparator_5_eq));
  Pull_Resistor pull_resistor_10 (.node(pull_resistor_10_node));
  Comparator #(.width(16)) comparator_6 (.a(transistor_4_out), .b(16'h84), .eq(pull_resistor_10_node));  // open: gt, lt
  Pull_Resistor pull_resistor_11 (.node(pull_resistor_11_node));
  Comparator #(.width(16)) comparator_7 (.a(transistor_4_out), .b(16'h96), .eq(pull_resistor_11_node));  // open: gt, lt
  Pull_Resistor pull_resistor_12 (.node(pull_resistor_12_node));
  Comparator #(.width(16)) comparator_8 (.a(transistor_4_out), .b(16'h9e), .eq(pull_resistor_12_node));  // open: gt, lt
  Comparator #(.width(16)) comparator_9 (.a(transistor_4_out), .b(16'ha0), .eq(comparator_9_eq));  // open: gt, lt
  Pull_Resistor pull_resistor_13 (.node(comparator_9_eq));
  Pull_Resistor pull_resistor_14 (.node(pull_resistor_14_node));
  Comparator #(.width(16)) comparator_10 (
    .a(transistor_4_out), .b(16'h9c), .eq(pull_resistor_14_node));  // open: gt, lt
  Pull_Resistor pull_resistor_15 (.node(pull_resistor_15_node));
  Comparator #(.width(16)) comparator_11 (
    .a(transistor_4_out), .b(16'hae), .eq(pull_resistor_15_node));  // open: gt, lt
  Pull_Resistor pull_resistor_16 (.node(pull_resistor_16_node));
  Comparator #(.width(16)) comparator_12 (
    .a(transistor_4_out), .b(16'hb0), .eq(pull_resistor_16_node));  // open: gt, lt
  Pull_Resistor pull_resistor_17 (.node(pull_resistor_17_node));
  Transistor #(.gate("br")) transistor_7 (.in(read_write), .out(pull_resistor_17_node), .gate(write_t));
  // ROM rom_1: pin names not known; wires that end beside it: transistor_4_out, code, word, controlled_buffer_2_out
  // RAM ram_1: pin names not known; wires that end beside it: transistor_4_out, transistor_6_out, data, clock, pull_resistor_17_node, controlled_buffer_2_out
  Register #(.width(16)) register_1 (.D(controlled_buffer_2_out), .Q(register_1_q), .clk(and_5_out));  // open: en, clr
  and and_5 (and_5_out, comparator_1_eq, data, transistor_3_out);
  Register #(.width(16)) register_2 (.D(controlled_buffer_2_out), .Q(register_2_q), .clk(and_6_out));  // open: en, clr
  and and_6 (and_6_out, pull_resistor_6_node, data, transistor_3_out);
  Register #(.width(16)) register_3 (.D(controlled_buffer_2_out), .Q(register_3_q), .clk(and_7_out));  // open: en, clr
  and and_7 (and_7_out, comparator_3_eq, data, transistor_3_out);
  Register #(.width(16)) register_4 (.D(controlled_buffer_2_out), .Q(register_4_q), .clk(and_8_out));  // open: en, clr
  and and_8 (and_8_out, pull_resistor_8_node, data, transistor_3_out);
  Register #(.width(16)) register_5 (.D(controlled_buffer_2_out), .Q(register_5_q), .clk(and_9_out));  // open: en, clr
  and and_9 (and_9_out, comparator_5_eq, data, transistor_3_out);
  Register #(.width(16)) register_6 (
    .D(controlled_buffer_2_out), .Q(register_6_q), .clk(and_10_out), .clr(end_cycle));  // open: en
  and and_10 (and_10_out, pull_resistor_10_node, data, transistor_3_out);
  Register #(.width(16)) register_7 (.D(controlled_buffer_2_out), .Q(register_7_q), .clk(and_11_out));  // open: en, clr
  and and_11 (and_11_out, pull_resistor_11_node, data, transistor_3_out);
  Register #(.width(16)) register_8 (.D(controlled_buffer_2_out), .Q(score), .clk(and_12_out));  // open: en, clr
  and and_12 (and_12_out, pull_resistor_12_node, data, transistor_3_out);
  Register #(.width(16)) register_9 (.D(controlled_buffer_2_out), .Q(register_9_q), .clk(and_13_out));  // open: en, clr
  and and_13 (and_13_out, comparator_9_eq, data, transistor_3_out);
  Register #(.width(16)) register_10 (
    .D(controlled_buffer_2_out), .Q(register_10_q), .clk(and_14_out));  // open: en, clr
  and and_14 (and_14_out, pull_resistor_14_node, data, transistor_3_out);
  Register #(.width(16)) register_11 (
    .D(controlled_buffer_2_out), .Q(register_11_q), .clk(and_15_out));  // open: en, clr
  and and_15 (and_15_out, pull_resistor_15_node, data, transistor_3_out);
  Register #(.width(16)) register_12 (.D(controlled_buffer_2_out), .Q(hp), .clk(and_16_out));  // open: en, clr
  and and_16 (and_16_out, pull_resistor_16_node, data, transistor_3_out);
  Transistor #(.\type ("n"), .width(16)) transistor_8 (.in(val), .out(controlled_buffer_2_out), .gate(write_t));
  assign id = drawing ? register_1_q : 16'bz;  // Controlled_Buffer controlled_buffer_3
  assign x = drawing ? register_2_q : 16'bz;  // Controlled_Buffer controlled_buffer_4
  assign y = drawing ? register_3_q : 16'bz;  // Controlled_Buffer controlled_buffer_5
  assign command = drawing ? register_4_q : 16'bz;  // Controlled_Buffer controlled_buffer_6
  Comparator #(.width(16), .mode("unsigned")) comparator_13 (
    .a(register_5_q), .b({16{1'b0}}), .eq(comparator_13_eq));  // open: gt, lt
  Bit_Extender #(.in_width(16), .out_width(1)) bit_extender_1 (.in(register_7_q), .out(bit_extender_1_out));
  Bit_Extender #(.in_width(16), .out_width(1)) bit_extender_2 (.in(register_9_q), .out(button));
  Bit_Extender #(.in_width(16), .out_width(1)) bit_extender_3 (.in(register_10_q), .out(gg));
  Bit_Extender #(.in_width(16), .out_width(1)) bit_extender_4 (.in(register_11_q), .out(win));
  not not_6 (collide, comparator_13_eq);
  Comparator #(.width(16), .mode("unsigned")) comparator_14 (
    .a(register_6_q), .b(16'h2), .eq(drawing));  // open: gt, lt
  Comparator #(.width(16), .mode("unsigned")) comparator_15 (
    .a(register_6_q), .b({16{1'b0}}), .eq(comparator_15_eq));  // open: gt, lt
  not not_7 (wait_int__checker, comparator_15_eq);
  not not_8 (not_8_out, drawing);
  xor xor_1 (run, not_8_out, bit_extender_1_out);
  Register #(.width(1)) u_initialized (.D(run), .Q(initialized), .clk(run));  // open: en, clr

  // Other names for the same wires on the sheet: checker = wait_int__checker; cl = clock; draw = drawing;
  //   end = end_cycle

  // Notes on the sheet:
  //   hold приостанавливает процессор
  //   write как hold но даёт возможность писать в ОЗУ
  //   cheker
  //   run
endmodule

module \Схема_расчётов  (
  input  [2:0] player_inp_x,
  input  shot,
  input  [2:0] player_inp_y,
  input  clock,
  input  drawing,
  output [4:0] X,
  output [4:0] Y,
  output [15:0] ID,
  output [15:0] Command,
  output [15:0] score,
  output [15:0] hp
);

  wire and_1_out, and_2_out, and_3_out, and_4_out, and_5_out, and_7_out, and_8_out, button, cdm16_1_drawing,
       collide, collide_check_enemy, collide_check_player, collide_check_wall, command_draw, command_show,
       comparator_5_eq, comparator_6_eq, comparator_7_eq, end_cycle, enemies_multiobject_1_ready,
       enemy_initing, hold, int_enemy, int_player, lose, not_1_out, or_5_out, player_initing,
       player_multiobject_1_ready, processor_draw, processor_drawing, register_1_q, register_3_q, run,
       \wait , wait_int, wall_initing, wall_multiobject_1_initing, wall_multiobject_1_ready,
       wall_multiobject_2_initing, wall_multiobject_2_ready, wall_multiobject_3_initing, win, write;
  wire [4:0] enemies_multiobject_1_debug__enemy_cout, wall_multiobject_1_debug__wall_cout,
       wall_multiobject_2_debug__wall_cout, wall_multiobject_3_debug__wall_cout;
  wire [5:0] player_multiobject_1_proc_command;
  wire [15:0] bit_extender_1_out, bit_extender_2_out, cdm16_1_hp, check2_writer_1_adr, check2_writer_1_val,
       collided, divider_1_out, divider_2_out, divider_3_out, divider_4_out, player_multiobject_1_x_2,
       player_multiobject_1_y_2, register_2_q, subtractor_1_out, subtractor_2_out, x_col, y_col;

  assign bit_extender_1_out = {{13{1'b0}}, player_inp_x};  // Bit_Extender bit_extender_1
  assign bit_extender_2_out = {{13{1'b0}}, player_inp_y};  // Bit_Extender bit_extender_2
  or or_1 (hold, wall_initing, enemy_initing, player_initing, processor_drawing);
  or or_2 (\wait , wait_int, write, drawing);
  or or_3 (end_cycle, win, lose);
  Pull_Resistor pull_resistor_1 (.node(collided));
  player_multiobject player_multiobject_1 (
    .draw(run), .ready(player_multiobject_1_ready), .id(ID), .x_2(player_multiobject_1_x_2),
    .y_2(player_multiobject_1_y_2), .x(subtractor_1_out), .y(subtractor_2_out), .command(Command),
    .\wait (\wait ), .clock(clock), .proc_command(player_multiobject_1_proc_command),
    .initing(player_initing), .end_cycle(end_cycle), .x_col(x_col), .y_col(y_col),
    .collide_check(collide_check_player), .collided(collided));
  Subtractor #(.width(16)) subtractor_1 (.a(bit_extender_1_out), .b(16'h4), .out(subtractor_1_out));  // open: bin, bout
  Subtractor #(.width(16)) subtractor_2 (.a(bit_extender_2_out), .b(16'h4), .out(subtractor_2_out));  // open: bin, bout
  // Probe on enemies_multiobject_1_debug__enemy_cout
  Comparator #(.width(16), .mode("unsigned")) comparator_1 (.a(Command), .b(16'h1), .eq(command_draw));  // open: gt, lt
  Pull_Resistor pull_resistor_2 (.node(command_draw));
  Pull_Resistor pull_resistor_3 (.node(command_show));
  Comparator #(.width(16), .mode("unsigned")) comparator_2 (.a(Command), .b(16'h2), .eq(command_show));  // open: gt, lt
  Pull_Resistor pull_resistor_4 (.node(int_player));
  Comparator #(.width(6), .mode("unsigned")) comparator_3 (
    .a(player_multiobject_1_proc_command), .b({6{1'b0}}), .eq(int_player));  // open: gt, lt
  Pull_Resistor pull_resistor_5 (.node(int_enemy));
  Comparator #(.width(6), .mode("unsigned")) comparator_4 (
    .a(player_multiobject_1_proc_command), .b(6'b000001), .eq(int_enemy));  // open: gt, lt
  enemies_multiobject enemies_multiobject_1 (
    .\wait (\wait ), .draw(player_multiobject_1_ready), .id(ID), .y(player_multiobject_1_y_2),
    .x(player_multiobject_1_x_2), .command(Command), .ready(enemies_multiobject_1_ready),
    .initing(enemy_initing), .collide_check(collide_check_enemy), .clock(clock),
    .DEBUG__enemy_cout(enemies_multiobject_1_debug__enemy_cout),
    .proc_command(player_multiobject_1_proc_command), .end_cycle(end_cycle), .x_col(x_col), .y_col(y_col),
    .collided(collided));  // open: speed
  // Probe on wall_multiobject_1_debug__wall_cout
  wall_multiobject wall_multiobject_1 (
    .\wait (\wait ), .draw(enemies_multiobject_1_ready), .x_col(x_col), .y_col(y_col), .id(ID),
    .y(player_multiobject_1_y_2), .x(player_multiobject_1_x_2), .command(Command),
    .ready(wall_multiobject_1_ready), .end_cycle(end_cycle), .collide_check(collide_check_wall),
    .collided(collided), .DEBUG__wall_cout(wall_multiobject_1_debug__wall_cout),
    .initing(wall_multiobject_1_initing), .clock(clock), .start_x(16'h8), .start_y(16'h32));
  or or_4 (wall_initing, wall_multiobject_1_initing, wall_multiobject_2_initing, wall_multiobject_3_initing);
  // Probe on wall_multiobject_2_debug__wall_cout
  wall_multiobject wall_multiobject_2 (
    .\wait (\wait ), .draw(wall_multiobject_1_ready), .x_col(x_col), .y_col(y_col), .id(ID),
    .y(player_multiobject_1_y_2), .x(player_multiobject_1_x_2), .command(Command),
    .ready(wall_multiobject_2_ready), .end_cycle(end_cycle), .collide_check(collide_check_wall),
    .collided(collided), .DEBUG__wall_cout(wall_multiobject_2_debug__wall_cout),
    .initing(wall_multiobject_2_initing), .clock(clock), .start_x(16'h1c), .start_y(16'h32));
  Register #(.width(1)) register_1 (
    .D(processor_draw), .Q(register_1_q), .clk(processor_draw), .clr(and_1_out));  // open: en
  and and_1 (and_1_out, ~drawing, register_1_q);  // AND_Gate
  check2_writer check2_writer_1 (
    .adr(check2_writer_1_adr), .val(check2_writer_1_val), .write(write), .run(and_1_out), .clock(clock));
  // Probe on wall_multiobject_3_debug__wall_cout
  wall_multiobject wall_multiobject_3 (
    .\wait (\wait ), .draw(wall_multiobject_2_ready), .x_col(x_col), .y_col(y_col), .id(ID),
    .y(player_multiobject_1_y_2), .x(player_multiobject_1_x_2), .command(Command), .ready(processor_draw),
    .end_cycle(end_cycle), .collide_check(collide_check_wall), .collided(collided),
    .DEBUG__wall_cout(wall_multiobject_3_debug__wall_cout), .initing(wall_multiobject_3_initing),
    .clock(clock), .start_x(16'h30), .start_y(16'h32));
  Register #(.width(16)) register_2 (.D(collided), .Q(register_2_q), .clk(not_1_out));  // open: en, clr
  not not_1 (not_1_out, comparator_5_eq);
  Comparator #(.width(16), .mode("unsigned")) comparator_5 (
    .a(collided), .b({16{1'b0}}), .eq(comparator_5_eq));  // open: gt, lt
  collision_writer collision_writer_1 (
    .adr(check2_writer_1_adr), .val(check2_writer_1_val), .write(write), .run(not_1_out), .clock(clock),
    .collided(register_2_q));
  and and_2 (and_2_out, command_draw, int_enemy);
  // Probe on ID
  // Probe on player_multiobject_1_x_2
  // Probe on player_multiobject_1_y_2
  // Probe on Command
  enemy_writer enemy_writer_1 (
    .x(player_multiobject_1_x_2), .y(player_multiobject_1_y_2), .adr(check2_writer_1_adr),
    .val(check2_writer_1_val), .write(write), .clock(clock), .run(and_2_out));
  Divider #(.width(16)) divider_1 (.a(player_multiobject_1_x_2), .b(16'h2), .out(divider_1_out));  // open: upper, rem
  and and_3 (and_3_out, command_draw, int_player);
  Bit_Extender #(.in_width(16), .out_width(5)) bit_extender_3 (.in(divider_1_out), .out(X));
  // Probe on X
  Divider #(.width(16)) divider_2 (.a(player_multiobject_1_y_2), .b(16'h2), .out(divider_2_out));  // open: upper, rem
  player_writer player_writer_1 (
    .x(player_multiobject_1_x_2), .y(player_multiobject_1_y_2), .adr(check2_writer_1_adr),
    .val(check2_writer_1_val), .write(write), .run(and_3_out), .clock(clock));
  // Probe on Y
  Bit_Extender #(.in_width(16), .out_width(5)) bit_extender_4 (.in(divider_2_out), .out(Y));
  win_multiobject win_multiobject_1 (
    .\wait (\wait ), .draw(win), .id(ID), .x(player_multiobject_1_x_2), .y(player_multiobject_1_y_2),
    .command(Command), .clock(clock));  // open: ready
  and and_4 (and_4_out, shot, ~button);  // AND_Gate
  and and_5 (and_5_out, register_3_q, ~write);  // AND_Gate
  Register #(.width(1)) register_3 (.D(and_4_out), .Q(register_3_q), .clk(and_4_out), .clr(and_5_out));  // open: en
  shot_writer shot_writer_1 (
    .adr(check2_writer_1_adr), .val(check2_writer_1_val), .run(and_5_out), .write(write), .clock(clock));
  lose_multiobject lose_multiobject_1 (
    .\wait (\wait ), .draw(lose), .id(ID), .x(player_multiobject_1_x_2), .y(player_multiobject_1_y_2),
    .command(Command), .clock(clock));  // open: ready
  Pull_Resistor pull_resistor_6 (.node(write));
  CDM16 cdm16_1 (
    .adr(check2_writer_1_adr), .val(check2_writer_1_val), .id(ID), .x(player_multiobject_1_x_2),
    .y(player_multiobject_1_y_2), .command(Command), .collide(collide), .write(write), .hold(hold),
    .clock(clock), .wait_int__checker(wait_int), .run(run), .drawing(cdm16_1_drawing), .score(score),
    .button(button), .gg(lose), .win(win), .hp(cdm16_1_hp), .end_cycle(end_cycle));
  Register #(.width(16)) x_3 (.D(divider_3_out), .Q(x_col), .clk(or_5_out));  // open: en, clr
  Divider #(.width(16)) divider_3 (.a(player_multiobject_1_x_2), .b(16'h2), .out(divider_3_out));  // open: upper, rem
  Comparator #(.width(16), .mode("unsigned")) comparator_6 (.a(ID), .b(16'hf), .eq(comparator_6_eq));  // open: gt, lt
  Pull_Resistor pull_resistor_7 (.node(comparator_6_eq));
  Comparator #(.width(16), .mode("unsigned")) comparator_7 (.a(ID), .b(16'ha), .eq(comparator_7_eq));  // open: gt, lt
  Pull_Resistor pull_resistor_8 (.node(comparator_7_eq));
  Divider #(.width(16)) divider_4 (.a(player_multiobject_1_y_2), .b(16'h2), .out(divider_4_out));  // open: upper, rem
  and and_6 (processor_drawing, cdm16_1_drawing, drawing);
  Register #(.width(16)) y_3 (.D(divider_4_out), .Q(y_col), .clk(or_5_out));  // open: en, clr
  and and_7 (and_7_out, command_draw, comparator_6_eq);
  and and_8 (and_8_out, command_draw, comparator_7_eq);
  or or_5 (or_5_out, and_8_out, and_7_out);
  D_Flip_Flop d_ff_1 (.clk(clock), .D(and_7_out), .Q(collide_check_player));  // open: Qn, preset, en, reset
  D_Flip_Flop d_ff_2 (.clk(clock), .D(and_8_out), .Q(collide_check_enemy));  // open: Qn, preset, en, reset
  D_Flip_Flop d_ff_3 (.clk(clock), .D(or_5_out), .Q(collide_check_wall));  // open: Qn, preset, en, reset

  assign hp = {16{1'b0}};

  // Other names for the same wires on the sheet: clk = clock
endmodule

module _32buffer_el (
  input  [31:0] \input ,
  input  _1___buffer_read,
  input  _1___buffer_write___clr,
  output [31:0] video,
  output [31:0] out_5
);

  wire [31:0] or_1_out;

  assign or_1_out = \input  | out_5;  // OR_Gate or_1, 32 bits wide
  Register #(.width(32)) buffer (
    .D(or_1_out), .Q(out_5), .clk(_1___buffer_read), .clr(_1___buffer_write___clr));  // open: en
  Register #(.width(32)) u_video (.D(out_5), .Q(video), .clk(_1___buffer_write___clr));  // open: en, clr
endmodule

module _32video_buffer_extendable (
  input  [31:0] in_1,
  input  w,
  input  block,
  input  [4:0] y,
  output [31:0] out_5,
  output [31:0] out_6,
  output [31:0] out_7,
  output [31:0] out_8,
  output [31:0] out_9,
  output [31:0] out_10,
  output [31:0] out_11,
  output [31:0] out_12,
  output [31:0] out_13,
  output [31:0] out_14,
  output [31:0] out_15,
  output [31:0] out_16,
  output [31:0] out_17,
  output [31:0] out_18,
  output [31:0] out_19,
  output [31:0] out_20,
  output [31:0] out_21,
  output [31:0] out_22,
  output [31:0] out_23,
  output [31:0] out_24,
  output [31:0] out_25,
  output [31:0] out_26,
  output [31:0] out_27,
  output [31:0] out_28,
  output [31:0] out_29,
  output [31:0] out_30,
  output [31:0] out_31,
  output [31:0] out_32,
  output [31:0] out_33,
  output [31:0] out_34,
  output [31:0] out_35,
  output [31:0] out_36
);

  wire _0, _1, _2, _3, _4, _5, _6, _7, _8, _9, _10, _11, _12, _13, _14, _15, _16, _17, _18, _19, _20, _21,
       _22, _23, _24, _25, _26, _27, _28, _29, _30, _31, clock_1_out, nor_1_out;
  wire [31:0] r0, r1, r2, r3, r4, r5, r6, r7, r8, r9, r10, r11, r12, r13, r14, r15, r16, r17, r18, r19, r20,
       r21, r22, r23, r24, r25, r26, r27, r28, r29, r30, r31;

  Demultiplexer #(.select(5), .disabled(0)) demultiplexer_1 (
    .out0(_0), .out1(_1), .out2(_2), .out3(_3), .out4(_4), .out5(_5), .out6(_6), .out7(_7), .out8(_8),
    .out9(_9), .out10(_10), .out11(_11), .out12(_12), .out13(_13), .out14(_14), .out15(_15), .out16(_16),
    .out17(_17), .out18(_18), .out19(_19), .out20(_20), .out21(_21), .out22(_22), .out23(_23), .out24(_24),
    .out25(_25), .out26(_26), .out27(_27), .out28(_28), .out29(_29), .out30(_30), .out31(_31), .in(1'b1),
    .sel(y), .en(nor_1_out));
  nor nor_1 (nor_1_out, block, clock_1_out);
  Clock clock_1 (.out(clock_1_out));
  _32buffer_el u_32buffer_el_1 (
    .\input (in_1), ._1___buffer_read(_0), .out_5(r0), .video(out_5), ._1___buffer_write___clr(w));
  _32buffer_el u_32buffer_el_2 (
    .\input (in_1), ._1___buffer_read(_1), .out_5(r1), .video(out_6), ._1___buffer_write___clr(w));
  _32buffer_el u_32buffer_el_3 (
    .\input (in_1), ._1___buffer_read(_2), .out_5(r2), .video(out_7), ._1___buffer_write___clr(w));
  _32buffer_el u_32buffer_el_4 (
    .\input (in_1), ._1___buffer_read(_3), .out_5(r3), .video(out_8), ._1___buffer_write___clr(w));
  _32buffer_el u_32buffer_el_5 (
    .\input (in_1), ._1___buffer_read(_4), .out_5(r4), .video(out_9), ._1___buffer_write___clr(w));
  _32buffer_el u_32buffer_el_6 (
    .\input (in_1), ._1___buffer_read(_5), .out_5(r5), .video(out_10), ._1___buffer_write___clr(w));
  _32buffer_el u_32buffer_el_7 (
    .\input (in_1), ._1___buffer_read(_6), .out_5(r6), .video(out_11), ._1___buffer_write___clr(w));
  _32buffer_el u_32buffer_el_8 (
    .\input (in_1), ._1___buffer_read(_7), .out_5(r7), .video(out_12), ._1___buffer_write___clr(w));
  _32buffer_el u_32buffer_el_9 (
    .\input (in_1), ._1___buffer_read(_8), .out_5(r8), .video(out_13), ._1___buffer_write___clr(w));
  _32buffer_el u_32buffer_el_10 (
    .\input (in_1), ._1___buffer_read(_9), .out_5(r9), .video(out_14), ._1___buffer_write___clr(w));
  _32buffer_el u_32buffer_el_11 (
    .\input (in_1), ._1___buffer_read(_10), .out_5(r10), .video(out_15), ._1___buffer_write___clr(w));
  _32buffer_el u_32buffer_el_12 (
    .\input (in_1), ._1___buffer_read(_11), .out_5(r11), .video(out_16), ._1___buffer_write___clr(w));
  _32buffer_el u_32buffer_el_13 (
    .\input (in_1), ._1___buffer_read(_12), .out_5(r12), .video(out_17), ._1___buffer_write___clr(w));
  _32buffer_el u_32buffer_el_14 (
    .\input (in_1), ._1___buffer_read(_13), .out_5(r13), .video(out_18), ._1___buffer_write___clr(w));
  _32buffer_el u_32buffer_el_15 (
    .\input (in_1), ._1___buffer_read(_14), .out_5(r14), .video(out_19), ._1___buffer_write___clr(w));
  _32buffer_el u_32buffer_el_16 (
    .\input (in_1), ._1___buffer_read(_15), .out_5(r15), .video(out_20), ._1___buffer_write___clr(w));
  _32buffer_el u_32buffer_el_17 (
    .\input (in_1), ._1___buffer_read(_16), .out_5(r16), .video(out_21), ._1___buffer_write___clr(w));
  _32buffer_el u_32buffer_el_18 (
    .\input (in_1), ._1___buffer_read(_17), .out_5(r17), .video(out_22), ._1___buffer_write___clr(w));
  _32buffer_el u_32buffer_el_19 (
    .\input (in_1), ._1___buffer_read(_18), .out_5(r18), .video(out_23), ._1___buffer_write___clr(w));
  _32buffer_el u_32buffer_el_20 (
    .\input (in_1), ._1___buffer_read(_19), .out_5(r19), .video(out_24), ._1___buffer_write___clr(w));
  _32buffer_el u_32buffer_el_21 (
    .\input (in_1), ._1___buffer_read(_20), .out_5(r20), .video(out_25), ._1___buffer_write___clr(w));
  _32buffer_el u_32buffer_el_22 (
    .\input (in_1), ._1___buffer_read(_21), .out_5(r21), .video(out_26), ._1___buffer_write___clr(w));
  _32buffer_el u_32buffer_el_23 (
    .\input (in_1), ._1___buffer_read(_22), .out_5(r22), .video(out_27), ._1___buffer_write___clr(w));
  _32buffer_el u_32buffer_el_24 (
    .\input (in_1), ._1___buffer_read(_23), .out_5(r23), .video(out_28), ._1___buffer_write___clr(w));
  _32buffer_el u_32buffer_el_25 (
    .\input (in_1), ._1___buffer_read(_24), .out_5(r24), .video(out_29), ._1___buffer_write___clr(w));
  _32buffer_el u_32buffer_el_26 (
    .\input (in_1), ._1___buffer_read(_25), .out_5(r25), .video(out_30), ._1___buffer_write___clr(w));
  _32buffer_el u_32buffer_el_27 (
    .\input (in_1), ._1___buffer_read(_26), .out_5(r26), .video(out_31), ._1___buffer_write___clr(w));
  _32buffer_el u_32buffer_el_28 (
    .\input (in_1), ._1___buffer_read(_27), .out_5(r27), .video(out_32), ._1___buffer_write___clr(w));
  _32buffer_el u_32buffer_el_29 (
    .\input (in_1), ._1___buffer_read(_28), .out_5(r28), .video(out_33), ._1___buffer_write___clr(w));
  _32buffer_el u_32buffer_el_30 (
    .\input (in_1), ._1___buffer_read(_29), .out_5(r29), .video(out_34), ._1___buffer_write___clr(w));
  _32buffer_el u_32buffer_el_31 (
    .\input (in_1), ._1___buffer_read(_30), .out_5(r30), .video(out_35), ._1___buffer_write___clr(w));
  _32buffer_el u_32buffer_el_32 (
    .\input (in_1), ._1___buffer_read(_31), .out_5(r31), .video(out_36), ._1___buffer_write___clr(w));

  // Other names for the same wires on the sheet: inp[31:0] = in_1

  // Notes on the sheet:
  //   block: pull=down
endmodule

module _32x32_ball (
  input  [5:0] in_1,
  input  [5:0] in_2,
  input  in_3,
  input  [4:0] in_4,
  output [31:0] out_5
);

  wire and_1_out, and_2_out, and_3_out, clock_1_out, clock_2_out, counter_1_q, counter_2_q, nor_1_out,
       nor_2_out, or_1_out, or_2_out;
  wire [4:0] bit_extender_1_out, bit_extender_2_out, xnor_1_out;
  wire [5:0] adder_1_out, adder_2_out, negator_1_out, negator_2_out, transistor_1_out, transistor_3_out, x_q,
       xv_q, y_q, yv_q;
  wire [31:0] shifter_1_out;

  // Probe on in_1
  // Probe on in_2
  Negator #(.width(6)) negator_1 (.in(in_1), .out(negator_1_out));
  Transistor #(.\type ("n"), .gate("br"), .width(6)) transistor_1 (
    .in(negator_1_out), .out(transistor_1_out), .gate(counter_2_q));
  Transistor #(.width(6)) transistor_2 (.in(in_1), .out(transistor_1_out), .gate(counter_2_q));
  Negator #(.width(6)) negator_2 (.in(in_2), .out(negator_2_out));
  Transistor #(.\type ("n"), .gate("br"), .width(6)) transistor_3 (
    .in(negator_2_out), .out(transistor_3_out), .gate(counter_1_q));
  Transistor #(.width(6)) transistor_4 (.in(in_2), .out(transistor_3_out), .gate(counter_1_q));
  Counter #(.width(1), .max('h1)) counter_1 (.Q(counter_1_q), .clk(or_1_out));  // open: load, D, count, carry, clr
  or or_1 (or_1_out, and_2_out, nor_1_out);
  nor nor_1 (nor_1_out, bit_extender_2_out[0], bit_extender_2_out[1], bit_extender_2_out[2], bit_extender_2_out[3], bit_extender_2_out[4]);
  Counter #(.width(1), .max('h1)) counter_2 (.Q(counter_2_q), .clk(or_2_out));  // open: load, D, count, carry, clr
  and and_1 (and_1_out, bit_extender_1_out[0], bit_extender_1_out[1], bit_extender_1_out[2], bit_extender_1_out[3], bit_extender_1_out[4]);
  or or_2 (or_2_out, and_1_out, nor_2_out);
  nor nor_2 (nor_2_out, bit_extender_1_out[0], bit_extender_1_out[1], bit_extender_1_out[2], bit_extender_1_out[3], bit_extender_1_out[4]);
  Register #(.width(6)) xv (.D(transistor_1_out), .Q(xv_q), .clk(clock_1_out));  // open: en, clr
  Clock clock_1 (.out(clock_1_out));
  Register #(.width(6)) yv (.D(transistor_3_out), .Q(yv_q), .clk(clock_2_out));  // open: en, clr
  Clock clock_2 (.out(clock_2_out));
  and and_2 (and_2_out, bit_extender_2_out[0], bit_extender_2_out[1], bit_extender_2_out[2], bit_extender_2_out[3], bit_extender_2_out[4]);
  Adder #(.width(6)) adder_1 (.a(xv_q), .b(x_q), .out(adder_1_out));  // open: cin, cout
  Adder #(.width(6)) adder_2 (.a(yv_q), .b(y_q), .out(adder_2_out));  // open: cin, cout
  Register #(.width(6)) x (.D(adder_1_out), .Q(x_q), .clk(in_3));  // open: en, clr
  Register #(.width(6)) y (.D(adder_2_out), .Q(y_q), .clk(in_3));  // open: en, clr
  Bit_Extender #(.in_width(6), .out_width(5)) bit_extender_1 (.in(x_q), .out(bit_extender_1_out));
  Bit_Extender #(.in_width(6), .out_width(5)) bit_extender_2 (.in(y_q), .out(bit_extender_2_out));
  Shifter #(.width(32), .shift("lr")) shifter_1 (.in(32'h80000000), .\dist (bit_extender_1_out), .out(shifter_1_out));
  assign xnor_1_out = ~(bit_extender_2_out ^ in_4);  // XNOR_Gate xnor_1, 5 bits wide
  and and_3 (and_3_out, xnor_1_out[0], xnor_1_out[1], xnor_1_out[2], xnor_1_out[3], xnor_1_out[4]);
  Transistor #(.gate("br"), .width(32)) transistor_5 (.in({32{1'b0}}), .out(out_5), .gate(and_3_out));
  Transistor #(.\type ("n"), .width(32)) transistor_6 (.in(shifter_1_out), .out(out_5), .gate(and_3_out));
endmodule

module _32_buffer_extendable__4 (
  input  [31:0] in_1,
  input  w,
  input  block,
  input  [4:0] y,
  output [31:0] out_5,
  output [31:0] out_6,
  output [31:0] out_7,
  output [31:0] out_8,
  output [31:0] out_9,
  output [31:0] out_10,
  output [31:0] out_11,
  output [31:0] out_12,
  output [31:0] out_13,
  output [31:0] out_14,
  output [31:0] out_15,
  output [31:0] out_16,
  output [31:0] out_17,
  output [31:0] out_18,
  output [31:0] out_19,
  output [31:0] out_20,
  output [31:0] out_21,
  output [31:0] out_22,
  output [31:0] out_23,
  output [31:0] out_24,
  output [31:0] out_25,
  output [31:0] out_26,
  output [31:0] out_27,
  output [31:0] out_28,
  output [31:0] out_29,
  output [31:0] out_30,
  output [31:0] out_31,
  output [31:0] out_32,
  output [31:0] out_33,
  output [31:0] out_34,
  output [31:0] out_35,
  output [31:0] out_36
);

  wire _0, _1, _2, _3, _4, _5, _6, _7, _8, _9, _10, _11, _12, _13, _14, _15, _16, _17, _18, _19, _20, _21,
       _22, _23, _24, _25, _26, _27, _28, _29, _30, _31, clock_1_out, nor_1_out;

  Demultiplexer #(.select(5), .disabled(0)) demultiplexer_1 (
    .out0(_0), .out1(_1), .out2(_2), .out3(_3), .out4(_4), .out5(_5), .out6(_6), .out7(_7), .out8(_8),
    .out9(_9), .out10(_10), .out11(_11), .out12(_12), .out13(_13), .out14(_14), .out15(_15), .out16(_16),
    .out17(_17), .out18(_18), .out19(_19), .out20(_20), .out21(_21), .out22(_22), .out23(_23), .out24(_24),
    .out25(_25), .out26(_26), .out27(_27), .out28(_28), .out29(_29), .out30(_30), .out31(_31), .in(1'b1),
    .sel(y), .en(nor_1_out));
  nor nor_1 (nor_1_out, block, clock_1_out);
  Clock clock_1 (.out(clock_1_out));
  _32buffer_el u_32buffer_el_1 (
    .\input (in_1), ._1___buffer_read(_0), .video(out_5), ._1___buffer_write___clr(w));  // open: out_5
  _32buffer_el u_32buffer_el_2 (
    .\input (in_1), ._1___buffer_read(_1), .video(out_6), ._1___buffer_write___clr(w));  // open: out_5
  _32buffer_el u_32buffer_el_3 (
    .\input (in_1), ._1___buffer_read(_2), .video(out_7), ._1___buffer_write___clr(w));  // open: out_5
  _32buffer_el u_32buffer_el_4 (
    .\input (in_1), ._1___buffer_read(_3), .video(out_8), ._1___buffer_write___clr(w));  // open: out_5
  _32buffer_el u_32buffer_el_5 (
    .\input (in_1), ._1___buffer_read(_4), .video(out_9), ._1___buffer_write___clr(w));  // open: out_5
  _32buffer_el u_32buffer_el_6 (
    .\input (in_1), ._1___buffer_read(_5), .video(out_10), ._1___buffer_write___clr(w));  // open: out_5
  _32buffer_el u_32buffer_el_7 (
    .\input (in_1), ._1___buffer_read(_6), .video(out_11), ._1___buffer_write___clr(w));  // open: out_5
  _32buffer_el u_32buffer_el_8 (
    .\input (in_1), ._1___buffer_read(_7), .video(out_12), ._1___buffer_write___clr(w));  // open: out_5
  _32buffer_el u_32buffer_el_9 (
    .\input (in_1), ._1___buffer_read(_8), .video(out_13), ._1___buffer_write___clr(w));  // open: out_5
  _32buffer_el u_32buffer_el_10 (
    .\input (in_1), ._1___buffer_read(_9), .video(out_14), ._1___buffer_write___clr(w));  // open: out_5
  _32buffer_el u_32buffer_el_11 (
    .\input (in_1), ._1___buffer_read(_10), .video(out_15), ._1___buffer_write___clr(w));  // open: out_5
  _32buffer_el u_32buffer_el_12 (
    .\input (in_1), ._1___buffer_read(_11), .video(out_16), ._1___buffer_write___clr(w));  // open: out_5
  _32buffer_el u_32buffer_el_13 (
    .\input (in_1), ._1___buffer_read(_12), .video(out_17), ._1___buffer_write___clr(w));  // open: out_5
  _32buffer_el u_32buffer_el_14 (
    .\input (in_1), ._1___buffer_read(_13), .video(out_18), ._1___buffer_write___clr(w));  // open: out_5
  _32buffer_el u_32buffer_el_15 (
    .\input (in_1), ._1___buffer_read(_14), .video(out_19), ._1___buffer_write___clr(w));  // open: out_5
  _32buffer_el u_32buffer_el_16 (
    .\input (in_1), ._1___buffer_read(_15), .video(out_20), ._1___buffer_write___clr(w));  // open: out_5
  _32buffer_el u_32buffer_el_17 (
    .\input (in_1), ._1___buffer_read(_16), .video(out_21), ._1___buffer_write___clr(w));  // open: out_5
  _32buffer_el u_32buffer_el_18 (
    .\input (in_1), ._1___buffer_read(_17), .video(out_22), ._1___buffer_write___clr(w));  // open: out_5
  _32buffer_el u_32buffer_el_19 (
    .\input (in_1), ._1___buffer_read(_18), .video(out_23), ._1___buffer_write___clr(w));  // open: out_5
  _32buffer_el u_32buffer_el_20 (
    .\input (in_1), ._1___buffer_read(_19), .video(out_24), ._1___buffer_write___clr(w));  // open: out_5
  _32buffer_el u_32buffer_el_21 (
    .\input (in_1), ._1___buffer_read(_20), .video(out_25), ._1___buffer_write___clr(w));  // open: out_5
  _32buffer_el u_32buffer_el_22 (
    .\input (in_1), ._1___buffer_read(_21), .video(out_26), ._1___buffer_write___clr(w));  // open: out_5
  _32buffer_el u_32buffer_el_23 (
    .\input (in_1), ._1___buffer_read(_22), .video(out_27), ._1___buffer_write___clr(w));  // open: out_5
  _32buffer_el u_32buffer_el_24 (
    .\input (in_1), ._1___buffer_read(_23), .video(out_28), ._1___buffer_write___clr(w));  // open: out_5
  _32buffer_el u_32buffer_el_25 (
    .\input (in_1), ._1___buffer_read(_24), .video(out_29), ._1___buffer_write___clr(w));  // open: out_5
  _32buffer_el u_32buffer_el_26 (
    .\input (in_1), ._1___buffer_read(_25), .video(out_30), ._1___buffer_write___clr(w));  // open: out_5
  _32buffer_el u_32buffer_el_27 (
    .\input (in_1), ._1___buffer_read(_26), .video(out_31), ._1___buffer_write___clr(w));  // open: out_5
  _32buffer_el u_32buffer_el_28 (
    .\input (in_1), ._1___buffer_read(_27), .video(out_32), ._1___buffer_write___clr(w));  // open: out_5
  _32buffer_el u_32buffer_el_29 (
    .\input (in_1), ._1___buffer_read(_28), .video(out_33), ._1___buffer_write___clr(w));  // open: out_5
  _32buffer_el u_32buffer_el_30 (
    .\input (in_1), ._1___buffer_read(_29), .video(out_34), ._1___buffer_write___clr(w));  // open: out_5
  _32buffer_el u_32buffer_el_31 (
    .\input (in_1), ._1___buffer_read(_30), .video(out_35), ._1___buffer_write___clr(w));  // open: out_5
  _32buffer_el u_32buffer_el_32 (
    .\input (in_1), ._1___buffer_read(_31), .video(out_36), ._1___buffer_write___clr(w));  // open: out_5

  // Other names for the same wires on the sheet: inp[31:0] = in_1

  // Notes on the sheet:
  //   block: pull=down
endmodule

module _64x64_ball (
  input  [6:0] vx,
  input  [6:0] vy,
  input  in_3,
  input  [5:0] cur_row,
  output [6:0] debug_x,
  output [6:0] debug_y,
  output [31:0] line_x1,
  output [31:0] line_x2
);

  wire and_1_out, and_2_out, and_3_out, and_4_out, and_5_out, clock_1_out, clock_2_out, counter_1_q,
       counter_2_q, nor_1_out, nor_2_out, not_1_out, not_2_out, or_1_out, or_2_out;
  wire [4:0] demultiplexer_1_out0, demultiplexer_1_out1;
  wire [5:0] bit_extender_1_out, bit_extender_2_out, xnor_1_out;
  wire [6:0] adder_1_out, adder_2_out, negator_1_out, negator_2_out, transistor_1_out, transistor_3_out,
       xv_q, yv_q;
  wire [31:0] shifter_1_out, shifter_2_out;

  // Probe on vx
  // Probe on vy
  Negator #(.width(7)) negator_1 (.in(vx), .out(negator_1_out));
  Transistor #(.\type ("n"), .gate("br"), .width(7)) transistor_1 (
    .in(negator_1_out), .out(transistor_1_out), .gate(counter_2_q));
  Transistor #(.width(7)) transistor_2 (.in(vx), .out(transistor_1_out), .gate(counter_2_q));
  Transistor #(.\type ("n"), .gate("br"), .width(7)) transistor_3 (
    .in(negator_2_out), .out(transistor_3_out), .gate(counter_1_q));
  Negator #(.width(7)) negator_2 (.in(vy), .out(negator_2_out));
  Transistor #(.width(7)) transistor_4 (.in(vy), .out(transistor_3_out), .gate(counter_1_q));
  Counter #(.width(1), .max('h1)) counter_1 (.Q(counter_1_q), .clk(or_1_out));  // open: load, D, count, carry, clr
  and and_1 (and_1_out, bit_extender_2_out[0], bit_extender_2_out[1], bit_extender_2_out[2], bit_extender_2_out[3], bit_extender_2_out[4], bit_extender_2_out[5]);
  or or_1 (or_1_out, and_1_out, nor_1_out);
  nor nor_1 (nor_1_out, bit_extender_2_out[0], bit_extender_2_out[1], bit_extender_2_out[2], bit_extender_2_out[3], bit_extender_2_out[4], bit_extender_2_out[5]);
  Counter #(.width(1), .max('h1)) counter_2 (.Q(counter_2_q), .clk(or_2_out));  // open: load, D, count, carry, clr
  and and_2 (and_2_out, bit_extender_1_out[0], bit_extender_1_out[1], bit_extender_1_out[2], bit_extender_1_out[3], bit_extender_1_out[4], bit_extender_1_out[5]);
  or or_2 (or_2_out, and_2_out, nor_2_out);
  nor nor_2 (nor_2_out, bit_extender_1_out[0], bit_extender_1_out[1], bit_extender_1_out[2], bit_extender_1_out[3], bit_extender_1_out[4], bit_extender_1_out[5]);
  Register #(.width(7)) xv (.D(transistor_1_out), .Q(xv_q), .clk(clock_1_out));  // open: en, clr
  Clock clock_1 (.out(clock_1_out));
  Register #(.width(7)) yv (.D(transistor_3_out), .Q(yv_q), .clk(clock_2_out));  // open: en, clr
  Clock clock_2 (.out(clock_2_out));
  Adder #(.width(7)) adder_1 (.a(xv_q), .b(debug_x), .out(adder_1_out));  // open: cin, cout
  Adder #(.width(7)) adder_2 (.a(yv_q), .b(debug_y), .out(adder_2_out));  // open: cin, cout
  Register #(.width(7)) x (.D(adder_1_out), .Q(debug_x), .clk(in_3));  // open: en, clr
  Register #(.width(7)) y (.D(adder_2_out), .Q(debug_y), .clk(in_3));  // open: en, clr
  // Probe on cur_row
  Demultiplexer #(.width(5), .enable("false")) demultiplexer_1 (
    .out0(demultiplexer_1_out0), .out1(demultiplexer_1_out1), .in(bit_extender_1_out[4:0]), .sel(not_1_out));
  not not_1 (not_1_out, bit_extender_1_out[5]);
  Bit_Extender #(.in_width(7), .out_width(6)) bit_extender_1 (.in(debug_x), .out(bit_extender_1_out));
  // Probe on bit_extender_2_out
  Bit_Extender #(.in_width(7), .out_width(6)) bit_extender_2 (.in(debug_y), .out(bit_extender_2_out));
  assign xnor_1_out = ~(bit_extender_2_out ^ cur_row);  // XNOR_Gate xnor_1, 6 bits wide
  Shifter #(.width(32), .shift("lr")) shifter_1 (.in(32'h80000000), .\dist (demultiplexer_1_out1), .out(shifter_1_out));
  not not_2 (not_2_out, bit_extender_1_out[5]);
  and and_3 (and_3_out, xnor_1_out[0], xnor_1_out[1], xnor_1_out[2], xnor_1_out[3], xnor_1_out[4], xnor_1_out[5]);
  and and_4 (and_4_out, and_3_out, not_2_out);
  Transistor #(.gate("br"), .width(32)) transistor_5 (.in({32{1'b0}}), .out(line_x1), .gate(and_4_out));
  Transistor #(.\type ("n"), .width(32)) transistor_6 (.in(shifter_1_out), .out(line_x1), .gate(and_4_out));
  and and_5 (and_5_out, bit_extender_1_out[5], and_3_out);
  Shifter #(.width(32), .shift("lr")) shifter_2 (.in(32'h80000000), .\dist (demultiplexer_1_out0), .out(shifter_2_out));
  Transistor #(.gate("br"), .width(32)) transistor_7 (.in({32{1'b0}}), .out(line_x2), .gate(and_5_out));
  Transistor #(.\type ("n"), .width(32)) transistor_8 (.in(shifter_2_out), .out(line_x2), .gate(and_5_out));
endmodule

module obj_module (
  input  [6:0] vx,
  input  [6:0] vy,
  input  update,
  input  [5:0] cur_line,
  output [31:0] line_x1,
  output [31:0] line_x2
);

  wire and_1_out, and_2_out, and_3_out, clock_1_out, clock_2_out, comparator_1_eq, comparator_1_gt,
       comparator_2_lt, comparator_3_lt, comparator_4_eq, comparator_4_gt, comparator_5_lt, comparator_6_eq,
       counter_1_q, counter_2_q, not_1_out, not_2_out, not_3_out, or_1_out, or_2_out, or_3_out, or_4_out,
       subtractor_2_bout, subtractor_3_bout;
  wire [4:0] bit_extender_3_out, bit_extender_4_out, multiplexer_1_out, multiplexer_2_out, multiplexer_4_out,
       subtractor_3_out, subtractor_4_out;
  wire [5:0] bit_extender_1_out, bit_extender_2_out, subtractor_1_out, subtractor_2_out;
  wire [6:0] adder_1_out, adder_2_out, negator_1_out, negator_2_out, transistor_1_out, transistor_3_out, x_q,
       xv_q, y_q, yv_q;
  wire [31:0] n32_bit_reverse_1_out_2, rom_1_data, shifter_1_out, shifter_2_out, shifter_3_out;

  // Probe on vx
  // Probe on vy
  Counter #(.width(1), .max('h1)) counter_1 (.Q(counter_1_q), .clk(or_1_out));  // open: load, D, count, carry, clr
  or or_1 (or_1_out, comparator_3_lt, or_3_out);
  Negator #(.width(7)) negator_1 (.in(vx), .out(negator_1_out));
  Transistor #(.\type ("n"), .gate("br"), .width(7)) transistor_1 (
    .in(negator_1_out), .out(transistor_1_out), .gate(counter_1_q));
  Transistor #(.width(7)) transistor_2 (.in(vx), .out(transistor_1_out), .gate(counter_1_q));
  Negator #(.width(7)) negator_2 (.in(vy), .out(negator_2_out));
  Counter #(.width(1), .max('h1)) counter_2 (.Q(counter_2_q), .clk(or_2_out));  // open: load, D, count, carry, clr
  or or_2 (or_2_out, or_4_out, comparator_2_lt);
  Register #(.width(7)) xv (.D(transistor_1_out), .Q(xv_q), .clk(clock_1_out));  // open: en, clr
  Clock clock_1 (.out(clock_1_out));
  Transistor #(.\type ("n"), .gate("br"), .width(7)) transistor_3 (
    .in(negator_2_out), .out(transistor_3_out), .gate(counter_2_q));
  Transistor #(.width(7)) transistor_4 (.in(vy), .out(transistor_3_out), .gate(counter_2_q));
  Register #(.width(7)) yv (.D(transistor_3_out), .Q(yv_q), .clk(clock_2_out));  // open: en, clr
  Clock clock_2 (.out(clock_2_out));
  Comparator #(.width(7)) comparator_1 (
    .a({7{1'b0}}), .b(y_q), .gt(comparator_1_gt), .eq(comparator_1_eq));  // open: lt
  Comparator #(.width(7)) comparator_2 (.a(7'b0111100), .b(y_q), .lt(comparator_2_lt));  // open: gt, eq
  Comparator #(.width(7)) comparator_3 (.a(7'b0111100), .b(x_q), .lt(comparator_3_lt));  // open: gt, eq
  or or_3 (or_3_out, comparator_4_gt, comparator_4_eq);
  Comparator #(.width(7)) comparator_4 (
    .a({7{1'b0}}), .b(x_q), .gt(comparator_4_gt), .eq(comparator_4_eq));  // open: lt
  Adder #(.width(7)) adder_1 (.a(xv_q), .b(x_q), .out(adder_1_out));  // open: cin, cout
  Adder #(.width(7)) adder_2 (.a(yv_q), .b(y_q), .out(adder_2_out));  // open: cin, cout
  or or_4 (or_4_out, comparator_1_gt, comparator_1_eq);
  Register #(.width(7)) x (.D(adder_1_out), .Q(x_q), .clk(update));  // open: en, clr
  Register #(.width(7)) y (.D(adder_2_out), .Q(y_q), .clk(update));  // open: en, clr
  Bit_Extender #(.in_width(7), .out_width(6)) bit_extender_1 (.in(x_q), .out(bit_extender_1_out));
  Bit_Extender #(.in_width(7), .out_width(6)) bit_extender_2 (.in(y_q), .out(bit_extender_2_out));
  Subtractor #(.width(6)) subtractor_1 (
    .a(cur_line), .b(bit_extender_2_out), .out(subtractor_1_out));  // open: bin, bout
  Subtractor #(.width(6)) subtractor_2 (
    .a(cur_line), .b(bit_extender_2_out), .out(subtractor_2_out), .bout(subtractor_2_bout));  // open: bin
  // Probe on cur_line
  Bit_Extender #(.in_width(6), .out_width(5)) bit_extender_3 (.in(subtractor_1_out), .out(bit_extender_3_out));
  Comparator #(.width(6), .mode("unsigned")) comparator_5 (
    .a(subtractor_2_out), .b(6'b100000), .lt(comparator_5_lt));  // open: gt, eq
  // Probe on bit_extender_1_out[4:0]
  not not_1 (not_1_out, bit_extender_1_out[5]);
  not not_2 (not_2_out, comparator_6_eq);
  Comparator #(.width(6), .mode("unsigned")) comparator_6 (
    .a(bit_extender_1_out), .b({6{1'b0}}), .eq(comparator_6_eq));  // open: gt, lt
  and and_1 (and_1_out, comparator_5_lt, not_3_out);
  not not_3 (not_3_out, subtractor_2_bout);
  ROM #(.addrWidth(5), .dataWidth(32)) rom_1 (.addr(bit_extender_3_out), .data(rom_1_data));  // open: sel
  assign bit_extender_4_out = {{4{1'b0}}, not_1_out};  // Bit_Extender bit_extender_4
  _32_bit_reverse u_32_bit_reverse_1 (.in_1(rom_1_data), .out_2(n32_bit_reverse_1_out_2));
  Subtractor #(.width(5)) subtractor_3 (
    .a(bit_extender_1_out[4:0]), .b(bit_extender_4_out), .out(subtractor_3_out), .bout(subtractor_3_bout));  // open: bin
  Multiplexer #(.width(5), .enable("false")) multiplexer_1 (
    .in0(subtractor_3_out), .in1({5{1'b0}}), .out(multiplexer_1_out), .sel(subtractor_3_bout));
  // Probe on {5{1'b1}}
  // Probe on subtractor_4_out
  Subtractor #(.width(5)) subtractor_4 (
    .a({5{1'b1}}), .b(multiplexer_1_out), .out(subtractor_4_out));  // open: bin, bout
  Shifter #(.width(32), .shift("lr")) shifter_1 (
    .in(n32_bit_reverse_1_out_2), .\dist (bit_extender_1_out[4:0]), .out(shifter_1_out));
  and and_2 (and_2_out, not_1_out, and_1_out);
  Multiplexer #(.width(5), .enable("false")) multiplexer_2 (
    .in0({5{1'b0}}), .in1(subtractor_4_out), .out(multiplexer_2_out), .sel(not_1_out));
  Multiplexer #(.width(32), .enable("false")) multiplexer_3 (
    .in0({32{1'b0}}), .in1(shifter_1_out), .out(line_x1), .sel(and_2_out));
  Shifter #(.width(32)) shifter_2 (.in(n32_bit_reverse_1_out_2), .\dist (multiplexer_2_out), .out(shifter_2_out));
  Multiplexer #(.width(5), .enable("false")) multiplexer_4 (
    .in0(bit_extender_1_out[4:0]), .in1({5{1'b0}}), .out(multiplexer_4_out), .sel(not_1_out));
  Shifter #(.width(32), .shift("lr")) shifter_3 (.in(shifter_2_out), .\dist (multiplexer_4_out), .out(shifter_3_out));
  and and_3 (and_3_out, not_2_out, and_1_out);
  Multiplexer #(.width(32), .enable("false")) multiplexer_5 (
    .in0({32{1'b0}}), .in1(shifter_3_out), .out(line_x2), .sel(and_3_out));

  // Notes on the sheet:
  //   address = y-line
  //   0 <= y-line < 32
  //   contents of rom_1 (hex, n*v repeats v):
  //   5 2 5
  //   +1 for shift left line x2
  //   to simulate shift by 32
  //   idk i just like that
  //   smth will work on line x2
  //   only if shift right > 0
  //   (still for simulate 32 shift)
  //   line x1 will work only if shift right < 32
  //   if x=0 shift left for line x2 must be 32 (with simulation of 32 shift)
  //   shift left for line x2
  //   shift rigth for line x2
  //   shift right works only if shift left = 0
endmodule

module _32_bit_reverse (
  input  [31:0] in_1,
  output [31:0] out_2
);


  assign out_2 = {in_1[0], in_1[1], in_1[2], in_1[3], in_1[4], in_1[5], in_1[6], in_1[7], in_1[8], in_1[9], in_1[10], in_1[11], in_1[12], in_1[13], in_1[14], in_1[15], in_1[16], in_1[17], in_1[18], in_1[19], in_1[20], in_1[21], in_1[22], in_1[23], in_1[24], in_1[25], in_1[26], in_1[27], in_1[28], in_1[29], in_1[30], in_1[31]};
endmodule

module abst_obj (
  input  write,
  input  [4:0] texture_line,
  input  [31:0] texture_input,
  input  [6:0] x,
  input  [6:0] y,
  input  draw,
  output [31:0] line_x1,
  output [31:0] line_x2,
  output [5:0] cur_line,
  output drawing
);

  wire and_1_out, and_2_out, and_3_out, comparator_1_lt, comparator_2_eq, counter_1_carry, drawing_q,
       not_1_out, not_2_out, not_4_out, not_5_out, not_6_out, register_1_q, subtractor_2_bout,
       subtractor_3_bout, transistor_3_out, x_upt, y_upd;
  wire [4:0] bit_extender_3_out, bit_extender_5_out, counter_1_q, multiplexer_1_out, multiplexer_2_out,
       multiplexer_4_out, subtractor_3_out, subtractor_4_out, transistor_1_out;
  wire [5:0] adder_1_out, bit_extender_1_out, bit_extender_2_out, bit_extender_4_out, subtractor_1_out,
       subtractor_2_out;
  wire [31:0] n32_bit_reverse_1_out_2, ram_1_data, shifter_1_out, shifter_2_out, shifter_3_out;

  // Probe on x
  // Probe on y
  Register #(.width(1)) register_1 (.D(draw), .Q(register_1_q), .clk(draw), .clr(counter_1_carry));  // open: en
  Register #(.width(1)) u_drawing (
    .D(register_1_q), .Q(drawing_q), .clk(not_1_out), .clr(counter_1_carry));  // open: en
  not not_1 (not_1_out, y_upd);
  or or_1 (drawing, register_1_q, drawing_q);
  Bit_Extender #(.in_width(7), .out_width(6)) bit_extender_1 (.in(x), .out(bit_extender_1_out));
  Bit_Extender #(.in_width(7), .out_width(6)) bit_extender_2 (.in(y), .out(bit_extender_2_out));
  // Probe on adder_1_out
  Subtractor #(.width(6)) subtractor_1 (
    .a(adder_1_out), .b(bit_extender_2_out), .out(subtractor_1_out));  // open: bin, bout
  Bit_Extender #(.in_width(6), .out_width(5)) bit_extender_3 (.in(subtractor_1_out), .out(bit_extender_3_out));
  Counter #(.width(5), .max('h3)) counter_1 (
    .count(drawing_q), .Q(counter_1_q), .carry(counter_1_carry), .clk(x_upt), .clr(counter_1_carry));  // open: load, D
  Subtractor #(.width(6)) subtractor_2 (
    .a(adder_1_out), .b(bit_extender_2_out), .out(subtractor_2_out), .bout(subtractor_2_bout));  // open: bin
  not not_2 (not_2_out, drawing_q);
  Register #(.width(6)) register_2 (.D(adder_1_out), .Q(cur_line), .clk(y_upd), .clr(not_2_out));  // open: en
  Transistor #(.gate("br"), .width(5)) transistor_1 (.in(texture_line), .out(transistor_1_out), .gate(register_1_q));
  Transistor #(.\type ("n"), .width(5)) transistor_2 (
    .in(bit_extender_3_out), .out(transistor_1_out), .gate(register_1_q));
  assign bit_extender_4_out = {{1{1'b0}}, counter_1_q};  // Bit_Extender bit_extender_4
  Comparator #(.width(6), .mode("unsigned")) comparator_1 (
    .a(subtractor_2_out), .b(6'b100000), .lt(comparator_1_lt));  // open: gt, eq
  not not_3 (x_upt, y_upd);
  Transistor #(.gate("br")) transistor_3 (.in(write), .out(transistor_3_out), .gate(register_1_q));
  // Probe on bit_extender_1_out[4:0]
  not not_4 (not_4_out, bit_extender_1_out[5]);
  Adder #(.width(6)) adder_1 (.a(bit_extender_2_out), .b(bit_extender_4_out), .out(adder_1_out));  // open: cin, cout
  not not_5 (not_5_out, comparator_2_eq);
  Comparator #(.width(6), .mode("unsigned")) comparator_2 (
    .a(bit_extender_1_out), .b({6{1'b0}}), .eq(comparator_2_eq));  // open: gt, lt
  and and_1 (and_1_out, comparator_1_lt, not_6_out);
  not not_6 (not_6_out, subtractor_2_bout);
  Clock clock_1 (.out(y_upd));
  assign bit_extender_5_out = {{4{1'b0}}, not_4_out};  // Bit_Extender bit_extender_5
  _32_bit_reverse u_32_bit_reverse_1 (.in_1(ram_1_data), .out_2(n32_bit_reverse_1_out_2));
  RAM #(.addrWidth(5), .dataWidth(32), .bus("separate")) ram_1 (
    .addr(transistor_1_out), .din(texture_input), .data(ram_1_data), .clk(transistor_3_out));  // open: str, sel, ld, clr
  Subtractor #(.width(5)) subtractor_3 (
    .a(bit_extender_1_out[4:0]), .b(bit_extender_5_out), .out(subtractor_3_out), .bout(subtractor_3_bout));  // open: bin
  Multiplexer #(.width(5), .enable("false")) multiplexer_1 (
    .in0(subtractor_3_out), .in1({5{1'b0}}), .out(multiplexer_1_out), .sel(subtractor_3_bout));
  // Probe on {5{1'b1}}
  // Probe on subtractor_4_out
  Subtractor #(.width(5)) subtractor_4 (
    .a({5{1'b1}}), .b(multiplexer_1_out), .out(subtractor_4_out));  // open: bin, bout
  Shifter #(.width(32), .shift("lr")) shifter_1 (
    .in(n32_bit_reverse_1_out_2), .\dist (bit_extender_1_out[4:0]), .out(shifter_1_out));
  Multiplexer #(.width(5), .enable("false")) multiplexer_2 (
    .in0({5{1'b0}}), .in1(subtractor_4_out), .out(multiplexer_2_out), .sel(not_4_out));
  and and_2 (and_2_out, not_4_out, register_1_q, drawing_q, and_1_out);
  Multiplexer #(.width(32), .enable("false")) multiplexer_3 (
    .in0({32{1'b0}}), .in1(shifter_1_out), .out(line_x1), .sel(and_2_out));
  Shifter #(.width(32)) shifter_2 (.in(n32_bit_reverse_1_out_2), .\dist (multiplexer_2_out), .out(shifter_2_out));
  Multiplexer #(.width(5), .enable("false")) multiplexer_4 (
    .in0(bit_extender_1_out[4:0]), .in1({5{1'b0}}), .out(multiplexer_4_out), .sel(not_4_out));
  Shifter #(.width(32), .shift("lr")) shifter_3 (.in(shifter_2_out), .\dist (multiplexer_4_out), .out(shifter_3_out));
  and and_3 (and_3_out, not_5_out, register_1_q, and_1_out, drawing_q);
  Multiplexer #(.width(32), .enable("false")) multiplexer_5 (
    .in0({32{1'b0}}), .in1(shifter_3_out), .out(line_x2), .sel(and_3_out));

  // Notes on the sheet:
  //   address = line-y
  //   0 <= y-line < 32
  //   +1 for shift left line x2
  //   to simulate shift by 32
  //   idk i just like that
  //   line x1 will work only if shift right < 32
  //   smth will work on line x2
  //   only if shift right > 0
  //   (still for simulate 32 shift)
  //   if x=0 shift left for line x2 must be 32 (with simulation of 32 shift)
  //   shift left for line x2
  //   shift rigth for line x2
  //   shift right works only if shift left = 0
endmodule

module player_multiobject (
  input  collide_check,
  input  [15:0] x,
  input  [15:0] y,
  input  \wait ,
  input  [15:0] x_col,
  input  end_cycle,
  input  draw,
  input  clock,
  input  [15:0] y_col,
  output [15:0] collided,
  output initing,
  output [15:0] id,
  output [15:0] x_2,
  output [15:0] y_2,
  output [15:0] command,
  output [5:0] proc_command,
  output ready
);

  wire and_1_out, and_2_out, and_3_out, collided_t, comparator_1_eq, comparator_2_lt, comparator_3_eq,
       comparator_3_gt, comparator_4_gt, counter_1_carry, d_ff_1_q, draw_t, init_step, not_1_out, not_3_out,
       not_4_out, not_5_out, not_6_out, not_7_out, not_8_out, or_1_out, or_2_out, register_1_q, register_2_q,
       transistor_1_out;
  wire [1:0] counter_1_q;
  wire [2:0] counter_2_q;
  wire [5:0] controlled_buffer_5_out;
  wire [15:0] adder_1_out, adder_2_out, controlled_buffer_1_out, controlled_buffer_2_out,
       controlled_buffer_3_out, controlled_buffer_4_out, divider_1_out, divider_2_out, multiplexer_2_out,
       multiplexer_3_out, multiplexer_4_out, subtractor_1_out, subtractor_2_out, x_t, y_t;

  Bit_Extender #(.in_width(2), .out_width(1)) bit_extender_1 (.in(counter_1_q), .out(init_step));
  Counter #(.width(2), .max('h2)) counter_1 (
    .Q(counter_1_q), .carry(counter_1_carry), .clk(clock), .clr(register_1_q));  // open: load, D, count
  or or_1 (or_1_out, end_cycle, ready);
  Register #(.width(1)) register_1 (.D(counter_1_carry), .Q(register_1_q), .clk(counter_1_carry));  // open: en, clr
  not not_1 (not_1_out, \wait );
  Register #(.width(1)) register_2 (.D(draw), .Q(register_2_q), .clk(draw), .clr(or_1_out));  // open: en
  not not_2 (initing, register_1_q);
  Counter #(.width(3), .max('h2)) counter_2 (
    .Q(counter_2_q), .carry(ready), .clk(transistor_1_out), .clr(ready));  // open: load, D, count
  Transistor #(.\type ("n")) transistor_1 (.in(clock), .out(transistor_1_out), .gate(and_1_out));
  and and_1 (and_1_out, not_1_out, register_2_q);
  Multiplexer #(.enable("false")) multiplexer_1 (.in0(register_2_q), .in1(init_step), .out(draw_t), .sel(initing));
  not not_3 (not_3_out, collided_t);
  Adder #(.width(16)) adder_1 (.a(x_t), .b(multiplexer_2_out), .out(adder_1_out));  // open: cin, cout
  Multiplexer #(.width(16), .enable("false")) multiplexer_2 (
    .in0(x), .in1(16'ha), .out(multiplexer_2_out), .sel(initing));
  Adder #(.width(16)) adder_2 (.a(y_t), .b(multiplexer_3_out), .out(adder_2_out));  // open: cin, cout
  Multiplexer #(.width(16), .enable("false")) multiplexer_3 (
    .in0(y), .in1(16'h38), .out(multiplexer_3_out), .sel(initing));
  Comparator #(.width(3), .mode("unsigned")) comparator_1 (
    .a(counter_2_q), .b(3'b001), .eq(comparator_1_eq));  // open: gt, lt
  Transistor #(.\type ("n"), .width(16)) transistor_2 (.in(16'h1), .out(collided), .gate(d_ff_1_q));
  D_Flip_Flop #(.trigger("falling")) d_ff_1 (
    .clk(clock), .D(collided_t), .Q(d_ff_1_q), .reset(not_3_out));  // open: Qn, preset, en
  Register #(.width(16)) u_x (.D(adder_1_out), .Q(x_t), .clk(draw_t));  // open: en, clr
  Register #(.width(16)) u_y (.D(adder_2_out), .Q(y_t), .clk(draw_t));  // open: en, clr
  Multiplexer #(.width(16), .enable("false")) multiplexer_4 (
    .in0({16{1'b0}}), .in1(16'h1), .out(multiplexer_4_out), .sel(comparator_1_eq));
  assign controlled_buffer_1_out = draw_t ? {16{1'b0}} : 16'bz;  // Controlled_Buffer controlled_buffer_1
  not not_4 (not_4_out, initing);
  assign controlled_buffer_2_out = draw_t ? x_t : 16'bz;  // Controlled_Buffer controlled_buffer_2
  not not_5 (not_5_out, initing);
  assign controlled_buffer_3_out = draw_t ? y_t : 16'bz;  // Controlled_Buffer controlled_buffer_3
  not not_6 (not_6_out, initing);
  assign controlled_buffer_4_out = draw_t ? multiplexer_4_out : 16'bz;  // Controlled_Buffer controlled_buffer_4
  not not_7 (not_7_out, initing);
  assign controlled_buffer_5_out = draw_t ? {6{1'b0}} : 6'bz;  // Controlled_Buffer controlled_buffer_5
  not not_8 (not_8_out, initing);
  assign id = not_4_out ? controlled_buffer_1_out : 16'bz;  // Controlled_Buffer controlled_buffer_6
  assign x_2 = not_5_out ? controlled_buffer_2_out : 16'bz;  // Controlled_Buffer controlled_buffer_7
  assign y_2 = not_6_out ? controlled_buffer_3_out : 16'bz;  // Controlled_Buffer controlled_buffer_8
  assign command = not_7_out ? controlled_buffer_4_out : 16'bz;  // Controlled_Buffer controlled_buffer_9
  assign proc_command = not_8_out ? controlled_buffer_5_out : 6'bz;  // Controlled_Buffer controlled_buffer_10
  Pull_Resistor pull_resistor_1 (.node(x_col));
  Pull_Resistor pull_resistor_2 (.node(y_col));
  // Probe on x_col
  Divider #(.width(16)) divider_1 (.a(x_t), .b(16'h2), .out(divider_1_out));  // open: upper, rem
  // Probe on y_col
  Divider #(.width(16)) divider_2 (.a(y_t), .b(16'h2), .out(divider_2_out));  // open: upper, rem
  Subtractor #(.width(16)) subtractor_1 (.a(x_col), .b(divider_1_out), .out(subtractor_1_out));  // open: bin, bout
  // Probe on subtractor_2_out
  Subtractor #(.width(16)) subtractor_2 (.a(y_col), .b(divider_2_out), .out(subtractor_2_out));  // open: bin, bout
  // Probe on 16'hfffd
  Comparator #(.width(16)) comparator_2 (.a(subtractor_1_out), .b(16'h3), .lt(comparator_2_lt));  // open: gt, eq
  Comparator #(.width(16)) comparator_3 (
    .a(subtractor_1_out), .b({16{1'b0}}), .gt(comparator_3_gt), .eq(comparator_3_eq));  // open: lt
  Comparator #(.width(16)) comparator_4 (.a(subtractor_2_out), .b(16'hfffd), .gt(comparator_4_gt));  // open: eq, lt
  and and_2 (and_2_out, comparator_2_lt, or_2_out);
  or or_2 (or_2_out, comparator_3_gt, comparator_3_eq);
  and and_3 (and_3_out, and_2_out, comparator_4_gt);
  and and_4 (collided_t, and_3_out, collide_check);

  // Other names for the same wires on the sheet: clk = clock
endmodule

module enemies_multiobject (
  input  collide_check,
  input  \wait ,
  input  end_cycle,
  input  draw,
  input  [15:0] x_col,
  input  clock,
  input  [15:0] y_col,
  output [15:0] collided,
  output [15:0] id,
  output initing,
  output [15:0] y,
  output [4:0] DEBUG__enemy_cout,
  output [15:0] x,
  output [15:0] command,
  output [5:0] proc_command,
  output ready,
  output [15:0] speed
);

  wire alive, and_1_out, and_2_out, and_4_out, and_5_out, and_6_out, and_7_out, and_8_out, and_9_out,
       and_10_out, and_11_out, collided_t, comparator_1_eq, comparator_1_gt, comparator_2_eq,
       comparator_2_lt, comparator_3_lt, comparator_5_eq, comparator_5_lt, comparator_6_eq, comparator_6_lt,
       comparator_7_eq, comparator_7_lt, counter_1_carry, draw_t, may_collide, multiplexer_1_out, not_1_out,
       not_2_out, not_4_out, not_5_out, not_6_out, not_7_out, or_1_out, or_2_out, or_4_out, or_5_out,
       or_6_out, or_7_out, or_8_out, or_9_out, or_10_out, or_11_out, or_12_out, pull_resistor_2_node,
       pull_resistor_3_node, register_1_q, register_3_q, register_4_q, register_5_q, register_8_q,
       register_9_q, texture_state, transistor_2_out, wait_t, xnor_1_out;
  wire [4:0] col_adr, counter_1_q;
  wire [15:0] adder_1_out, adder_2_out, adder_3_out, adder_4_out, adder_5_out, adder_6_out, adder_7_out,
       adder_8_out, bit_extender_1_out, controlled_buffer_1_out, divider_1_out, divider_1_rem, divider_2_out,
       divider_3_out, divider_4_out, divider_4_rem, divider_5_out, divider_5_rem, multiplexer_4_out,
       multiplexer_5_out, multiplexer_6_out, multiplexer_7_out, multiplier_1_out, multiplier_2_out,
       multiplier_3_out, multiplier_4_out, multiplier_5_out, negator_1_out, negator_2_out, register_10_q,
       register_11_q, subtractor_1_out, subtractor_2_out, subtractor_3_out, x_t, y_t;

  or or_1 (or_1_out, end_cycle, ready);
  not not_1 (not_1_out, may_collide);
  Register #(.width(1)) register_1 (.D(or_2_out), .Q(register_1_q), .clk(clock));  // open: en, clr
  or or_2 (or_2_out, collide_check, \wait );
  Register #(.width(1)) register_2 (.D(register_3_q), .Q(draw_t), .clk(clock), .clr(or_1_out));  // open: en
  Register #(.width(1)) register_3 (.D(draw), .Q(register_3_q), .clk(draw), .clr(or_1_out));  // open: en
  and and_1 (and_1_out, collided_t, alive);
  D_Flip_Flop #(.trigger("falling")) d_ff_1 (
    .clk(clock), .D(may_collide), .Q(collided_t), .reset(not_1_out));  // open: Qn, preset, en
  Counter #(.width(5), .max('he)) counter_1 (
    .Q(counter_1_q), .carry(counter_1_carry), .clk(not_2_out));  // open: load, D, count, clr
  or or_3 (wait_t, register_1_q, or_2_out);
  Transistor #(.\type ("n"), .width(16)) transistor_1 (.in(16'h2), .out(collided), .gate(and_1_out));
  not not_2 (not_2_out, multiplexer_1_out);
  Multiplexer #(.enable("false")) multiplexer_1 (
    .in0(clock), .in1(transistor_2_out), .out(multiplexer_1_out), .sel(register_4_q));
  Transistor #(.\type ("n"), .gate("br")) transistor_2 (.in(or_4_out), .out(transistor_2_out), .gate(draw_t));
  Pull_Resistor pull_resistor_1 (.node(transistor_2_out));
  or or_4 (or_4_out, wait_t, and_2_out);
  not not_3 (initing, register_4_q);
  Multiplexer #(.width(5), .enable("false")) multiplexer_2 (
    .in0(counter_1_q), .in1(col_adr), .out(DEBUG__enemy_cout), .sel(may_collide));
  not not_4 (not_4_out, counter_1_carry);
  Register #(.width(1)) register_4 (.D(not_4_out), .Q(register_4_q), .clk(not_4_out));  // open: en, clr
  and and_2 (and_2_out, ~clock, ~and_4_out);  // AND_Gate
  Multiplexer #(.width(16), .enable("false")) multiplexer_3 (
    .in0(multiplexer_4_out), .in1({16{1'b0}}), .out(speed), .sel(initing));
  Pull_Resistor pull_resistor_2 (.node(pull_resistor_2_node));
  Transistor #(.gate("br")) transistor_3 (.in(1'b1), .out(pull_resistor_2_node), .gate(register_4_q));
  Negator #(.width(16)) negator_1 (.in(16'h1), .out(negator_1_out));
  assign bit_extender_1_out = {{11{1'b0}}, DEBUG__enemy_cout};  // Bit_Extender bit_extender_1
  xnor xnor_1 (xnor_1_out, collided_t, register_4_q);
  Register #(.width(1)) register_5 (.D(not_4_out), .Q(register_5_q), .clk(not_4_out), .clr(register_5_q));  // open: en
  // Probe on subtractor_3_out
  Adder #(.width(16)) adder_1 (.a(x_t), .b(multiplexer_4_out), .out(adder_1_out));  // open: cin, cout
  Multiplexer #(.width(16), .enable("false")) multiplexer_4 (
    .in0(16'h1), .in1(negator_1_out), .out(multiplexer_4_out), .sel(register_8_q));
  Adder #(.width(16)) adder_2 (.a(16'h2), .b(y_t), .out(adder_2_out));  // open: cin, cout
  RAM #(.addrWidth(5), .dataWidth(1), .bus("separate")) ram_1 (
    .addr(DEBUG__enemy_cout), .din(pull_resistor_2_node), .data(alive), .str(xnor_1_out), .clk(clock));  // open: sel, ld, clr
  and and_3 (ready, register_5_q, draw_t);
  Register #(.width(16)) register_6 (.D(adder_1_out), .Q(x_t), .clk(ready));  // open: en, clr
  Register #(.width(16)) register_7 (.D(adder_2_out), .Q(y_t), .clk(and_5_out));  // open: en, clr
  Divider #(.width(16)) divider_1 (
    .a(bit_extender_1_out), .b(16'h5), .out(divider_1_out), .rem(divider_1_rem));  // open: upper
  and and_4 (and_4_out, alive, register_4_q);
  Comparator #(.width(16), .mode("unsigned")) comparator_1 (
    .a(x_t), .b(subtractor_3_out), .gt(comparator_1_gt), .eq(comparator_1_eq));  // open: lt
  and and_5 (and_5_out, register_9_q, ready);
  and and_6 (and_6_out, and_4_out, or_6_out);
  not not_5 (not_5_out, clock);
  Counter #(.width(1), .max('h1)) counter_2 (
    .Q(texture_state), .clk(register_5_q));  // open: load, D, count, carry, clr
  // Probe on negator_2_out
  or or_5 (or_5_out, comparator_1_gt, comparator_1_eq);
  Adder #(.width(16)) adder_3 (.a(16'h3), .b(divider_1_out), .out(adder_3_out));  // open: cin, cout
  Adder #(.width(16)) adder_4 (.a(16'h6), .b(divider_1_out), .out(adder_4_out));  // open: cin, cout
  Multiplier #(.width(16)) multiplier_1 (.a(divider_1_out), .b(16'ha), .out(multiplier_1_out));  // open: cin, cout
  Multiplier #(.width(16)) multiplier_2 (.a(divider_1_rem), .b(16'ha), .out(multiplier_2_out));  // open: cin, cout
  Multiplexer #(.width(16), .enable("false")) multiplexer_5 (
    .in0({16{1'b0}}), .in1(16'h1), .out(multiplexer_5_out), .sel(and_6_out));
  or or_6 (or_6_out, not_5_out, wait_t);
  Comparator #(.width(16)) comparator_2 (
    .a(x_t), .b(negator_2_out), .eq(comparator_2_eq), .lt(comparator_2_lt));  // open: gt
  or or_7 (or_7_out, comparator_2_eq, comparator_2_lt);
  or or_8 (or_8_out, or_5_out, and_7_out);
  Multiplexer #(.width(16), .enable("false")) multiplexer_6 (
    .in0(adder_3_out), .in1(adder_4_out), .out(multiplexer_6_out), .sel(texture_state));
  Adder #(.width(16)) adder_5 (.a(y_t), .b(multiplier_1_out), .out(adder_5_out));  // open: cin, cout
  Adder #(.width(16)) adder_6 (.a(x_t), .b(multiplier_2_out), .out(adder_6_out));  // open: cin, cout
  assign controlled_buffer_1_out = alive ? divider_1_rem : 16'bz;  // Controlled_Buffer controlled_buffer_1
  assign proc_command = draw_t ? 6'b000001 : 6'bz;  // Controlled_Buffer controlled_buffer_2
  Register #(.width(1)) register_8 (.D(or_5_out), .Q(register_8_q), .clk(or_5_out), .clr(and_7_out));  // open: en
  Register #(.width(1)) register_9 (.D(or_8_out), .Q(register_9_q), .clk(or_8_out), .clr(and_5_out));  // open: en
  assign id = draw_t ? multiplexer_6_out : 16'bz;  // Controlled_Buffer controlled_buffer_3
  assign y = draw_t ? adder_5_out : 16'bz;  // Controlled_Buffer controlled_buffer_4
  assign x = draw_t ? adder_6_out : 16'bz;  // Controlled_Buffer controlled_buffer_5
  assign command = draw_t ? multiplexer_5_out : 16'bz;  // Controlled_Buffer controlled_buffer_6
  and and_7 (and_7_out, or_7_out, register_8_q);
  Comparator #(.width(16), .mode("unsigned")) comparator_3 (
    .a(controlled_buffer_1_out), .b(register_11_q), .lt(comparator_3_lt));  // open: gt, eq
  Register #(.width(16)) register_10 (
    .D(controlled_buffer_1_out), .Q(register_10_q), .clk(and_8_out), .clr(not_6_out));  // open: en
  and and_8 (and_8_out, pull_resistor_3_node, wait_t);
  Pull_Resistor pull_resistor_3 (.node(pull_resistor_3_node));
  Comparator #(.width(16), .mode("unsigned")) comparator_4 (
    .a(controlled_buffer_1_out), .b(register_10_q), .gt(pull_resistor_3_node));  // open: eq, lt
  Pull_Resistor pull_resistor_4 (.node(x_col));
  Pull_Resistor pull_resistor_5 (.node(y_col));
  Register #(.width(16)) register_11 (.D(multiplexer_7_out), .Q(register_11_q), .clk(or_9_out));  // open: en, clr
  Multiplexer #(.width(16), .enable("false")) multiplexer_7 (
    .in0(16'h30), .in1(controlled_buffer_1_out), .out(multiplexer_7_out), .sel(draw_t));
  or or_9 (or_9_out, and_9_out, and_10_out);
  and and_9 (and_9_out, comparator_3_lt, wait_t);
  Pull_Resistor pull_resistor_6 (.node(comparator_3_lt));
  not not_6 (not_6_out, draw_t);
  Adder #(.width(16)) adder_7 (.a(16'h1), .b(register_10_q), .out(adder_7_out));  // open: cin, cout
  Divider #(.width(16)) divider_2 (.a(x_t), .b(16'h2), .out(divider_2_out));  // open: upper, rem
  Divider #(.width(16)) divider_3 (.a(y_t), .b(16'h2), .out(divider_3_out));  // open: upper, rem
  not not_7 (not_7_out, draw_t);
  Multiplier #(.width(16)) multiplier_3 (.a(16'h8), .b(adder_7_out), .out(multiplier_3_out));  // open: cin, cout
  // Probe on x_col
  // Probe on subtractor_1_out
  Subtractor #(.width(16)) subtractor_1 (.a(x_col), .b(divider_2_out), .out(subtractor_1_out));  // open: bin, bout
  // Probe on divider_2_out
  // Probe on divider_4_rem
  Subtractor #(.width(16)) subtractor_2 (.a(y_col), .b(divider_3_out), .out(subtractor_2_out));  // open: bin, bout
  and and_10 (and_10_out, not_7_out, clock);
  Negator #(.width(16)) negator_2 (.in(multiplier_4_out), .out(negator_2_out));
  Multiplier #(.width(16)) multiplier_4 (.a(register_11_q), .b(16'ha), .out(multiplier_4_out));  // open: cin, cout
  Subtractor #(.width(16)) subtractor_3 (.a(16'h3b), .b(multiplier_3_out), .out(subtractor_3_out));  // open: bin, bout
  Divider #(.width(16)) divider_4 (
    .a(subtractor_1_out), .b(16'h5), .out(divider_4_out), .rem(divider_4_rem));  // open: upper
  Divider #(.width(16)) divider_5 (
    .a(subtractor_2_out), .b(16'h5), .out(divider_5_out), .rem(divider_5_rem));  // open: upper
  Comparator #(.width(16), .mode("unsigned")) comparator_5 (
    .a(divider_4_rem), .b(16'h2), .eq(comparator_5_eq), .lt(comparator_5_lt));  // open: gt
  or or_10 (or_10_out, comparator_5_eq, comparator_5_lt);
  Multiplier #(.width(16)) multiplier_5 (.a(divider_5_out), .b(16'h5), .out(multiplier_5_out));  // open: cin, cout
  Comparator #(.width(16), .mode("unsigned")) comparator_6 (
    .a(divider_5_rem), .b(16'h2), .eq(comparator_6_eq), .lt(comparator_6_lt));  // open: gt
  or or_11 (or_11_out, comparator_6_eq, comparator_6_lt);
  // Probe on divider_4_out
  and and_11 (and_11_out, or_10_out, or_11_out);
  // Probe on multiplier_5_out
  // Probe on adder_8_out
  Adder #(.width(16)) adder_8 (.a(divider_4_out), .b(multiplier_5_out), .out(adder_8_out));  // open: cin, cout
  Bit_Extender #(.in_width(16), .out_width(5)) bit_extender_2 (.in(adder_8_out), .out(col_adr));
  Comparator #(.width(16), .mode("unsigned")) comparator_7 (
    .a(adder_8_out), .b(16'he), .eq(comparator_7_eq), .lt(comparator_7_lt));  // open: gt
  or or_12 (or_12_out, comparator_7_eq, comparator_7_lt);
  and and_12 (may_collide, or_12_out, and_11_out, collide_check);

  // Other names for the same wires on the sheet: clk = clock

  // Notes on the sheet:
  //   enemy matrix
  //   enemies in row
  //   base texture id1
  //   base texture id2
  //   rows delta
  //   columns delta
  //   output X
  //   output Y
endmodule

module wall_multiobject (
  input  collide_check,
  input  \wait ,
  input  end_cycle,
  input  draw,
  input  [15:0] start_x,
  input  [15:0] x_col,
  input  [15:0] start_y,
  input  clock,
  input  [15:0] y_col,
  output [15:0] collided,
  output [15:0] id,
  output initing,
  output [15:0] y,
  output [4:0] DEBUG__wall_cout,
  output [15:0] x,
  output [15:0] command,
  output ready
);

  wire alive, and_1_out, and_2_out, and_3_out, and_5_out, and_6_out, and_7_out, block, comparator_1_eq,
       comparator_2_eq, comparator_3_gt, comparator_4_lt, comparator_5_eq, comparator_5_lt,
       controlled_buffer_1_out, counter_1_carry, d_ff_1_q, draw_t, may_collide, multiplexer_1_out, not_1_out,
       not_2_out, not_4_out, not_5_out, not_6_out, not_7_out, not_9_out, or_1_out, or_2_out, or_4_out,
       or_5_out, or_6_out, register_1_q, register_2_q, register_4_q, register_5_q, texture_state,
       transistor_1_out, wait_t, xnor_1_out;
  wire [1:0] multiplexer_3_out, ram_1_data, subtractor_1_out, transistor_3_out;
  wire [4:0] col_adr, counter_1_q;
  wire [15:0] adder_1_out, adder_2_out, bit_extender_1_out, bit_extender_2_out, divider_1_out, divider_2_out,
       divider_3_out, multiplexer_4_out, multiplier_1_out, subtractor_2_out, subtractor_3_out, x_t, y_t;

  not not_1 (not_1_out, may_collide);
  or or_1 (or_1_out, end_cycle, ready);
  and and_1 (and_1_out, d_ff_1_q, alive);
  D_Flip_Flop #(.trigger("falling")) d_ff_1 (
    .clk(clock), .D(may_collide), .Q(d_ff_1_q), .reset(not_1_out));  // open: Qn, preset, en
  Register #(.width(1)) register_1 (.D(or_2_out), .Q(register_1_q), .clk(clock));  // open: en, clr
  or or_2 (or_2_out, collide_check, \wait );
  Register #(.width(1)) register_2 (.D(draw), .Q(register_2_q), .clk(draw), .clr(or_1_out));  // open: en
  Register #(.width(1)) register_3 (.D(register_2_q), .Q(draw_t), .clk(clock), .clr(or_1_out));  // open: en
  Counter #(.width(5), .max('h1)) counter_1 (
    .Q(counter_1_q), .carry(counter_1_carry), .clk(not_2_out));  // open: load, D, count, clr
  or or_3 (wait_t, register_1_q, or_2_out);
  and and_2 (and_2_out, and_1_out, ~block);  // AND_Gate
  D_Flip_Flop #(.trigger("falling")) d_ff_2 (.clk(clock), .D(and_1_out), .Q(block));  // open: Qn, preset, en, reset
  not not_2 (not_2_out, multiplexer_1_out);
  Multiplexer #(.enable("false")) multiplexer_1 (
    .in0(clock), .in1(transistor_1_out), .out(multiplexer_1_out), .sel(register_4_q));
  Transistor #(.\type ("n"), .gate("br")) transistor_1 (.in(or_4_out), .out(transistor_1_out), .gate(draw_t));
  Pull_Resistor pull_resistor_1 (.node(transistor_1_out));
  or or_4 (or_4_out, wait_t, and_3_out);
  Transistor #(.\type ("n"), .width(16)) transistor_2 (.in(16'h3), .out(collided), .gate(and_2_out));
  not not_3 (initing, register_4_q);
  Multiplexer #(.width(5), .enable("false")) multiplexer_2 (
    .in0(counter_1_q), .in1(col_adr), .out(DEBUG__wall_cout), .sel(may_collide));
  not not_4 (not_4_out, counter_1_carry);
  Register #(.width(1)) register_4 (.D(not_4_out), .Q(register_4_q), .clk(not_4_out));  // open: en, clr
  and and_3 (and_3_out, ~clock, ~and_5_out);  // AND_Gate
  Transistor #(.gate("br"), .width(2)) transistor_3 (.in(2'b11), .out(transistor_3_out), .gate(register_4_q));
  Transistor #(.\type ("n"), .width(2)) transistor_4 (
    .in(multiplexer_3_out), .out(transistor_3_out), .gate(register_4_q));
  assign bit_extender_1_out = {{11{1'b0}}, DEBUG__wall_cout};  // Bit_Extender bit_extender_1
  assign controlled_buffer_1_out = not_5_out ? clock : 1'bz;  // Controlled_Buffer controlled_buffer_1
  xnor xnor_1 (xnor_1_out, may_collide, register_4_q);
  Register #(.width(1)) register_5 (.D(not_4_out), .Q(register_5_q), .clk(not_4_out), .clr(register_5_q));  // open: en
  RAM #(.addrWidth(5), .dataWidth(2), .bus("separate")) ram_1 (
    .addr(DEBUG__wall_cout), .din(transistor_3_out), .data(ram_1_data), .str(xnor_1_out),
    .clk(controlled_buffer_1_out));  // open: sel, ld, clr
  not not_5 (not_5_out, block);
  Comparator #(.width(2), .mode("unsigned")) comparator_1 (
    .a(ram_1_data), .b(2'b00), .eq(comparator_1_eq));  // open: gt, lt
  and and_4 (ready, register_5_q, draw_t);
  Register #(.width(16)) register_6 (.D(start_x), .Q(x_t), .clk(not_6_out));  // open: en, clr
  not not_6 (not_6_out, initing);
  Register #(.width(16)) register_7 (.D(start_y), .Q(y_t), .clk(not_7_out));  // open: en, clr
  not not_7 (not_7_out, initing);
  assign bit_extender_2_out = {{14{1'b0}}, ram_1_data};  // Bit_Extender bit_extender_2
  Subtractor #(.width(2)) subtractor_1 (.a(ram_1_data), .b(2'b01), .out(subtractor_1_out));  // open: bin, bout
  Multiplexer #(.width(2), .enable("false")) multiplexer_3 (
    .in0(subtractor_1_out), .in1(2'b00), .out(multiplexer_3_out), .sel(comparator_1_eq));
  not not_8 (alive, comparator_2_eq);
  Comparator #(.width(2), .mode("unsigned")) comparator_2 (
    .a(ram_1_data), .b(2'b00), .eq(comparator_2_eq));  // open: gt, lt
  and and_5 (and_5_out, alive, register_4_q);
  Counter #(.width(1), .max('h1)) counter_2 (
    .Q(texture_state), .clk(register_5_q));  // open: load, D, count, carry, clr
  Multiplexer #(.width(16), .enable("false")) multiplexer_4 (
    .in0({16{1'b0}}), .in1(16'h1), .out(multiplexer_4_out), .sel(and_6_out));
  and and_6 (and_6_out, and_5_out, or_5_out);
  or or_5 (or_5_out, not_9_out, wait_t);
  not not_9 (not_9_out, clock);
  Adder #(.width(16)) adder_1 (.a(16'h10), .b(bit_extender_2_out), .out(adder_1_out));  // open: cin, cout
  Multiplier #(.width(16)) multiplier_1 (.a(bit_extender_1_out), .b(16'h4), .out(multiplier_1_out));  // open: cin, cout
  assign id = draw_t ? adder_1_out : 16'bz;  // Controlled_Buffer controlled_buffer_2
  assign y = draw_t ? y_t : 16'bz;  // Controlled_Buffer controlled_buffer_3
  assign x = draw_t ? adder_2_out : 16'bz;  // Controlled_Buffer controlled_buffer_4
  Adder #(.width(16)) adder_2 (.a(x_t), .b(multiplier_1_out), .out(adder_2_out));  // open: cin, cout
  assign command = draw_t ? multiplexer_4_out : 16'bz;  // Controlled_Buffer controlled_buffer_5
  Pull_Resistor pull_resistor_2 (.node(x_col));
  Pull_Resistor pull_resistor_3 (.node(y_col));
  // Probe on x_col
  Subtractor #(.width(16)) subtractor_2 (.a(x_col), .b(divider_1_out), .out(subtractor_2_out));  // open: bin, bout
  Divider #(.width(16)) divider_1 (.a(x_t), .b(16'h2), .out(divider_1_out));  // open: upper, rem
  // Probe on divider_1_out
  Subtractor #(.width(16)) subtractor_3 (.a(y_col), .b(divider_2_out), .out(subtractor_3_out));  // open: bin, bout
  Divider #(.width(16)) divider_2 (.a(y_t), .b(16'h2), .out(divider_2_out));  // open: upper, rem
  // Probe on subtractor_2_out
  Divider #(.width(16)) divider_3 (.a(subtractor_2_out), .b(16'h2), .out(divider_3_out));  // open: upper, rem
  Comparator #(.width(16)) comparator_3 (.a(subtractor_3_out), .b(16'hfffd), .gt(comparator_3_gt));  // open: eq, lt
  Comparator #(.width(16)) comparator_4 (.a(subtractor_3_out), .b(16'h3), .lt(comparator_4_lt));  // open: gt, eq
  // Probe on divider_3_out
  // Probe on divider_3_out
  and and_7 (and_7_out, comparator_3_gt, comparator_4_lt);
  Comparator #(.width(16), .mode("unsigned")) comparator_5 (
    .a(divider_3_out), .b(16'h1), .eq(comparator_5_eq), .lt(comparator_5_lt));  // open: gt
  Bit_Extender #(.in_width(16), .out_width(5)) bit_extender_3 (.in(divider_3_out), .out(col_adr));
  or or_6 (or_6_out, comparator_5_eq, comparator_5_lt);
  and and_8 (may_collide, or_6_out, collide_check, and_7_out);

  // Other names for the same wires on the sheet: clk = clock

  // Notes on the sheet:
  //   wall matrix
  //   base texture id
  //   columns delta
  //   output Y
  //   output X
endmodule

module win_multiobject (
  input  \wait ,
  input  draw,
  input  clock,
  output [15:0] id,
  output [15:0] x,
  output [15:0] y,
  output [15:0] command,
  output ready
);

  wire and_1_out, comparator_1_eq, draw_t, not_1_out, not_2_out, register_1_q, transistor_1_out;
  wire [3:0] counter_1_q;
  wire [15:0] bit_extender_1_out, multiplexer_1_out, multiplexer_2_out, multiplexer_3_out, multiplexer_4_out;

  Register #(.width(1)) register_1 (.D(draw), .Q(register_1_q), .clk(draw), .clr(ready));  // open: en
  Register #(.width(1)) register_2 (.D(register_1_q), .Q(draw_t), .clk(not_1_out), .clr(ready));  // open: en
  not not_1 (not_1_out, clock);
  not not_2 (not_2_out, \wait );
  Counter #(.width(4), .max('h5)) counter_1 (
    .Q(counter_1_q), .carry(ready), .clk(transistor_1_out), .clr(ready));  // open: load, D, count
  Transistor #(.\type ("n")) transistor_1 (.in(clock), .out(transistor_1_out), .gate(and_1_out));
  and and_1 (and_1_out, not_2_out, draw_t);
  Multiplexer #(.width(16), .enable("false")) multiplexer_1 (
    .in0(16'hb), .in1(16'hc), .out(multiplexer_1_out), .sel(counter_1_q[1]));
  Multiplexer #(.width(16), .enable("false")) multiplexer_2 (
    .in0(16'h1a), .in1(16'h20), .out(multiplexer_2_out), .sel(counter_1_q[1]));
  Comparator #(.width(4), .mode("unsigned")) comparator_1 (
    .a(counter_1_q), .b(4'b0000), .eq(comparator_1_eq));  // open: gt, lt
  assign bit_extender_1_out = {{15{1'b0}}, counter_1_q[0]};  // Bit_Extender bit_extender_1
  assign id = draw_t ? multiplexer_1_out : 16'bz;  // Controlled_Buffer controlled_buffer_1
  assign x = draw_t ? 16'h10 : 16'bz;  // Controlled_Buffer controlled_buffer_2
  assign y = draw_t ? multiplexer_2_out : 16'bz;  // Controlled_Buffer controlled_buffer_3
  Multiplexer #(.width(16), .enable("false")) multiplexer_3 (
    .in0(multiplexer_4_out), .in1(16'h2), .out(multiplexer_3_out), .sel(comparator_1_eq));
  Multiplexer #(.width(16), .enable("false")) multiplexer_4 (
    .in0(bit_extender_1_out), .in1(16'h2), .out(multiplexer_4_out), .sel(counter_1_q[2]));
  assign command = draw_t ? multiplexer_3_out : 16'bz;  // Controlled_Buffer controlled_buffer_4

  // Other names for the same wires on the sheet: clk = clock
endmodule

module lose_multiobject (
  input  \wait ,
  input  draw,
  input  clock,
  output [15:0] id,
  output [15:0] x,
  output [15:0] y,
  output [15:0] command,
  output ready
);

  wire and_1_out, comparator_1_eq, draw_t, not_1_out, not_2_out, register_2_q, transistor_1_out;
  wire [3:0] counter_1_q;
  wire [15:0] bit_extender_1_out, multiplexer_1_out, multiplexer_2_out, multiplexer_3_out, multiplexer_4_out;

  Register #(.width(1)) register_1 (.D(register_2_q), .Q(draw_t), .clk(not_1_out), .clr(ready));  // open: en
  Register #(.width(1)) register_2 (.D(draw), .Q(register_2_q), .clk(draw), .clr(ready));  // open: en
  not not_1 (not_1_out, clock);
  not not_2 (not_2_out, \wait );
  Counter #(.width(4), .max('hf)) counter_1 (
    .Q(counter_1_q), .carry(ready), .clk(transistor_1_out), .clr(ready));  // open: load, D, count
  Transistor #(.\type ("n")) transistor_1 (.in(clock), .out(transistor_1_out), .gate(and_1_out));
  and and_1 (and_1_out, not_2_out, draw_t);
  Multiplexer #(.width(16), .enable("false")) multiplexer_1 (
    .in0(16'hd), .in1(16'he), .out(multiplexer_1_out), .sel(counter_1_q[1]));
  Multiplexer #(.width(16), .enable("false")) multiplexer_2 (
    .in0(16'h1a), .in1(16'h20), .out(multiplexer_2_out), .sel(counter_1_q[1]));
  Comparator #(.width(4), .mode("unsigned")) comparator_1 (
    .a(counter_1_q), .b(4'b0000), .eq(comparator_1_eq));  // open: gt, lt
  assign bit_extender_1_out = {{15{1'b0}}, counter_1_q[0]};  // Bit_Extender bit_extender_1
  assign id = draw_t ? multiplexer_1_out : 16'bz;  // Controlled_Buffer controlled_buffer_1
  assign x = draw_t ? 16'h8 : 16'bz;  // Controlled_Buffer controlled_buffer_2
  assign y = draw_t ? multiplexer_2_out : 16'bz;  // Controlled_Buffer controlled_buffer_3
  Multiplexer #(.width(16), .enable("false")) multiplexer_3 (
    .in0(multiplexer_4_out), .in1(16'h2), .out(multiplexer_3_out), .sel(comparator_1_eq));
  Multiplexer #(.width(16), .enable("false")) multiplexer_4 (
    .in0(bit_extender_1_out), .in1(16'h2), .out(multiplexer_4_out), .sel(counter_1_q[2]));
  assign command = draw_t ? multiplexer_3_out : 16'bz;  // Controlled_Buffer controlled_buffer_4

  // Other names for the same wires on the sheet: clk = clock
endmodule

module enemy_writer (
  input  [15:0] y,
  input  [15:0] x,
  input  run,
  input  clock,
  output [15:0] val,
  output [15:0] adr,
  output write
);

  wire activate_q, counter_1_carry, not_1_out, not_2_out, pull_resistor_1_node, writing;
  wire [2:0] counter_1_q, random_1_out;
  wire [15:0] bit_extender_1_out, multiplexer_1_out, multiplexer_2_out;

  Pull_Resistor pull_resistor_1 (.node(pull_resistor_1_node));
  assign pull_resistor_1_node = writing ? clock : 1'bz;  // Controlled_Buffer controlled_buffer_1
  Random #(.width(3)) random_1 (.clk(pull_resistor_1_node), .out(random_1_out));  // open: next, clr
  assign bit_extender_1_out = {{13{1'b0}}, random_1_out};  // Bit_Extender bit_extender_1
  Counter #(.width(3), .max('h5)) counter_1 (
    .Q(counter_1_q), .carry(counter_1_carry), .clk(not_1_out), .clr(not_2_out));  // open: load, D, count
  not not_1 (not_1_out, clock);
  Multiplexer #(.select(3), .width(16), .enable("false")) multiplexer_1 (
    .in0({16{1'b0}}), .in1(16'h80), .in2(16'h82), .in3(16'hac), .in4(16'h84), .out(multiplexer_1_out),
    .sel(counter_1_q));  // open: in5, in6, in7
  Multiplexer #(.select(3), .width(16), .enable("false")) multiplexer_2 (
    .in0({16{1'b0}}), .in1(x), .in2(y), .in3(bit_extender_1_out), .in4(16'h1), .out(multiplexer_2_out),
    .sel(counter_1_q));  // open: in5, in6, in7
  D_Flip_Flop activate (.clk(run), .D(run), .Q(activate_q), .reset(counter_1_carry));  // open: Qn, preset, en
  // Probe on multiplexer_1_out
  assign adr = writing ? multiplexer_1_out : 16'bz;  // Controlled_Buffer controlled_buffer_2
  assign val = writing ? multiplexer_2_out : 16'bz;  // Controlled_Buffer controlled_buffer_3
  // Probe on multiplexer_2_out
  not not_2 (not_2_out, writing);
  buf buffer_1 (write, writing);
  D_Flip_Flop #(.trigger("falling")) synchronizer (
    .clk(clock), .D(activate_q), .Q(writing), .reset(counter_1_carry));  // open: Qn, preset, en

  // Other names for the same wires on the sheet: clk = clock

  // Notes on the sheet:
  //   buffer_1 drives only 1 and floats otherwise
endmodule

module check2_writer (
  input  run,
  input  clock,
  output [15:0] adr,
  output [15:0] val,
  output write
);

  wire activator_q, counter_1_carry, not_1_out, writing;
  wire [1:0] counter_1_q;
  wire [15:0] multiplexer_1_out, multiplexer_2_out;

  Counter #(.width(2), .max('h2)) counter_1 (
    .Q(counter_1_q), .carry(counter_1_carry), .clk(clock), .clr(not_1_out));  // open: load, D, count
  Multiplexer #(.select(2), .width(16), .enable("false")) multiplexer_1 (
    .in0({16{1'b0}}), .in1(16'h84), .out(multiplexer_1_out), .sel(counter_1_q));  // open: in2, in3
  Multiplexer #(.select(2), .width(16), .enable("false")) multiplexer_2 (
    .in0({16{1'b0}}), .in1(16'h2), .out(multiplexer_2_out), .sel(counter_1_q));  // open: in2, in3
  D_Flip_Flop activator (.clk(run), .D(run), .Q(activator_q), .reset(counter_1_carry));  // open: Qn, preset, en
  assign adr = writing ? multiplexer_1_out : 16'bz;  // Controlled_Buffer controlled_buffer_1
  // Probe on multiplexer_1_out
  assign val = writing ? multiplexer_2_out : 16'bz;  // Controlled_Buffer controlled_buffer_2
  // Probe on multiplexer_2_out
  not not_1 (not_1_out, writing);
  D_Flip_Flop #(.trigger("falling")) synchronizer (
    .clk(clock), .D(activator_q), .Q(writing), .reset(counter_1_carry));  // open: Qn, preset, en
  buf buffer_1 (write, writing);

  // Other names for the same wires on the sheet: clk = clock

  // Notes on the sheet:
  //   buffer_1 drives only 1 and floats otherwise
endmodule

module speed_writer (
  input  [15:0] speed,
  input  clock,
  input  run,
  output [15:0] adr,
  output [15:0] val,
  output write
);

  wire activator_q, and_1_out, comparator_1_eq, counter_1_carry, not_1_out, not_2_out, writing;
  wire [1:0] counter_1_q;
  wire [15:0] multiplexer_1_out, multiplexer_2_out, register_1_q;

  Register #(.width(16)) register_1 (.D(speed), .Q(register_1_q), .clk(and_1_out));  // open: en, clr
  and and_1 (and_1_out, run, not_1_out);
  Counter #(.width(2), .max('h2)) counter_1 (
    .Q(counter_1_q), .carry(counter_1_carry), .clk(clock), .clr(not_2_out));  // open: load, D, count
  Comparator #(.width(16), .mode("unsigned")) comparator_1 (
    .a(register_1_q), .b(speed), .eq(comparator_1_eq));  // open: gt, lt
  not not_1 (not_1_out, comparator_1_eq);
  Multiplexer #(.select(2), .width(16), .enable("false")) multiplexer_1 (
    .in0({16{1'b0}}), .in1(16'h98), .out(multiplexer_1_out), .sel(counter_1_q));  // open: in2, in3
  Multiplexer #(.select(2), .width(16), .enable("false")) multiplexer_2 (
    .in0({16{1'b0}}), .in1(speed), .out(multiplexer_2_out), .sel(counter_1_q));  // open: in2, in3
  assign adr = writing ? multiplexer_1_out : 16'bz;  // Controlled_Buffer controlled_buffer_1
  // Probe on multiplexer_1_out
  assign val = writing ? multiplexer_2_out : 16'bz;  // Controlled_Buffer controlled_buffer_2
  // Probe on multiplexer_2_out
  not not_2 (not_2_out, writing);
  D_Flip_Flop activator (
    .clk(and_1_out), .D(and_1_out), .Q(activator_q), .reset(counter_1_carry));  // open: Qn, preset, en
  buf buffer_1 (write, writing);
  D_Flip_Flop #(.trigger("falling")) synchronizer (
    .clk(clock), .D(activator_q), .Q(writing), .reset(counter_1_carry));  // open: Qn, preset, en

  // Other names for the same wires on the sheet: clk = clock

  // Notes on the sheet:
  //   buffer_1 drives only 1 and floats otherwise
endmodule

module shot_writer (
  input  run,
  input  clock,
  output [15:0] adr,
  output [15:0] val,
  output write
);

  wire activator_q, counter_1_carry, not_1_out, not_2_out, writing;
  wire [1:0] counter_1_q;
  wire [15:0] multiplexer_1_out, multiplexer_2_out;

  Counter #(.width(2), .max('h2)) counter_1 (
    .Q(counter_1_q), .carry(counter_1_carry), .clk(not_1_out), .clr(not_2_out));  // open: load, D, count
  not not_1 (not_1_out, clock);
  Multiplexer #(.select(2), .width(16), .enable("false")) multiplexer_1 (
    .in0({16{1'b0}}), .in1(16'ha0), .out(multiplexer_1_out), .sel(counter_1_q));  // open: in2, in3
  Multiplexer #(.select(2), .width(16), .enable("false")) multiplexer_2 (
    .in0({16{1'b0}}), .in1(16'h1), .out(multiplexer_2_out), .sel(counter_1_q));  // open: in2, in3
  assign adr = writing ? multiplexer_1_out : 16'bz;  // Controlled_Buffer controlled_buffer_1
  // Probe on multiplexer_1_out
  assign val = writing ? multiplexer_2_out : 16'bz;  // Controlled_Buffer controlled_buffer_2
  // Probe on multiplexer_2_out
  not not_2 (not_2_out, writing);
  D_Flip_Flop activator (.clk(run), .D(run), .Q(activator_q), .reset(counter_1_carry));  // open: Qn, preset, en
  buf buffer_1 (write, writing);
  D_Flip_Flop #(.trigger("falling")) synchronizer (
    .clk(clock), .D(activator_q), .Q(writing), .reset(counter_1_carry));  // open: Qn, preset, en

  // Other names for the same wires on the sheet: clk = clock

  // Notes on the sheet:
  //   buffer_1 drives only 1 and floats otherwise
endmodule
module player_writer (
  input  [15:0] x,
  input  [15:0] y,
  input  run,
  input  clock,
  output [15:0] adr,
  output [15:0] val,
  output write
);

  wire activator_q, counter_1_carry, not_1_out, not_2_out, writing;
  wire [1:0] bit_extender_1_out;
  wire [2:0] counter_1_q;
  wire [15:0] multiplexer_1_out, multiplexer_2_out;

  Counter #(.width(3), .max('h3)) counter_1 (
    .Q(counter_1_q), .carry(counter_1_carry), .clk(not_1_out), .clr(not_2_out));  // open: load, D, count
  not not_1 (not_1_out, clock);
  // Probe on x
  // Probe on y
  Bit_Extender #(.in_width(3), .out_width(2)) bit_extender_1 (.in(counter_1_q), .out(bit_extender_1_out));
  Multiplexer #(.select(2), .width(16), .enable("false")) multiplexer_1 (
    .in0({16{1'b0}}), .in1(16'ha8), .in2(16'haa), .out(multiplexer_1_out), .sel(bit_extender_1_out));  // open: in3
  Multiplexer #(.select(2), .width(16), .enable("false")) multiplexer_2 (
    .in0({16{1'b0}}), .in1(x), .in2(y), .out(multiplexer_2_out), .sel(bit_extender_1_out));  // open: in3
  D_Flip_Flop activator (.clk(run), .D(run), .Q(activator_q), .reset(counter_1_carry));  // open: Qn, preset, en
  assign adr = writing ? multiplexer_1_out : 16'bz;  // Controlled_Buffer controlled_buffer_1
  // Probe on multiplexer_1_out
  assign val = writing ? multiplexer_2_out : 16'bz;  // Controlled_Buffer controlled_buffer_2
  // Probe on multiplexer_2_out
  not not_2 (not_2_out, writing);
  D_Flip_Flop #(.trigger("falling")) synchronizer (
    .clk(clock), .D(activator_q), .Q(writing), .reset(counter_1_carry));  // open: Qn, preset, en
  buf buffer_1 (write, writing);

  // Other names for the same wires on the sheet: clk = clock

  // Notes on the sheet:
  //   buffer_1 drives only 1 and floats otherwise
endmodule

module collision_writer (
  input  [15:0] collided,
  input  run,
  input  clock,
  output [15:0] adr,
  output [15:0] val,
  output write
);

  wire activator_q, counter_1_carry, not_1_out, not_2_out, writing;
  wire [1:0] counter_1_q;
  wire [15:0] multiplexer_1_out, multiplexer_2_out;

  Counter #(.width(2), .max('h2)) counter_1 (
    .Q(counter_1_q), .carry(counter_1_carry), .clk(not_1_out), .clr(not_2_out));  // open: load, D, count
  not not_1 (not_1_out, clock);
  Multiplexer #(.select(2), .width(16), .enable("false")) multiplexer_1 (
    .in0({16{1'b0}}), .in1(16'h94), .out(multiplexer_1_out), .sel(counter_1_q));  // open: in2, in3
  Multiplexer #(.select(2), .width(16), .enable("false")) multiplexer_2 (
    .in0({16{1'b0}}), .in1(collided), .out(multiplexer_2_out), .sel(counter_1_q));  // open: in2, in3
  assign adr = writing ? multiplexer_1_out : 16'bz;  // Controlled_Buffer controlled_buffer_1
  // Probe on multiplexer_1_out
  assign val = writing ? multiplexer_2_out : 16'bz;  // Controlled_Buffer controlled_buffer_2
  // Probe on multiplexer_2_out
  not not_2 (not_2_out, writing);
  D_Flip_Flop activator (.clk(run), .D(run), .Q(activator_q), .reset(counter_1_carry));  // open: Qn, preset, en
  buf buffer_1 (write, writing);
  D_Flip_Flop #(.trigger("falling")) synchronizer (
    .clk(clock), .D(activator_q), .Q(writing), .reset(counter_1_carry));  // open: Qn, preset, en

  // Other names for the same wires on the sheet: clk = clock

  // Notes on the sheet:
  //   buffer_1 drives only 1 and floats otherwise
endmodule

module simple_drawer_32x32 (
  input  [4:0] texture_line,
  input  [31:0] texture_input,
  input  [4:0] x,
  input  [4:0] y,
  output [4:0] cur_line,
  output [31:0] line_x1
);

  wire [31:0] n32_bit_reverse_1_out_2;

  // Probe on x
  // Probe on y
  Adder #(.width(5)) adder_1 (.a(texture_line), .b(y), .out(cur_line));  // open: cin, cout
  _32_bit_reverse u_32_bit_reverse_1 (.in_1(texture_input), .out_2(n32_bit_reverse_1_out_2));
  Pull_Resistor pull_resistor_1 (.node(x));
  Shifter #(.width(32), .shift("lr")) shifter_1 (.in(n32_bit_reverse_1_out_2), .\dist (x), .out(line_x1));
endmodule

module video_buffer_32x32 (
  input  [31:0] in_1,
  input  write,
  input  show,
  input  [4:0] y,
  output [31:0] out_5,
  output [31:0] out_6,
  output [31:0] out_7,
  output [31:0] out_8,
  output [31:0] out_9,
  output [31:0] out_10,
  output [31:0] out_11,
  output [31:0] out_12,
  output [31:0] out_13,
  output [31:0] out_14,
  output [31:0] out_15,
  output [31:0] out_16,
  output [31:0] out_17,
  output [31:0] out_18,
  output [31:0] out_19,
  output [31:0] out_20,
  output [31:0] out_21,
  output [31:0] out_22,
  output [31:0] out_23,
  output [31:0] out_24,
  output [31:0] out_25,
  output [31:0] out_26,
  output [31:0] out_27,
  output [31:0] out_28,
  output [31:0] out_29,
  output [31:0] out_30,
  output [31:0] out_31,
  output [31:0] out_32,
  output [31:0] out_33,
  output [31:0] out_34,
  output [31:0] out_35,
  output [31:0] out_36
);

  wire _0, _1, _2, _3, _4, _5, _6, _7, _8, _9, _10, _11, _12, _13, _14, _15, _16, _17, _18, _19, _20, _21,
       _22, _23, _24, _25, _26, _27, _28, _29, _30, _31;
  wire [31:0] r0, r1, r2, r3, r4, r5, r6, r7, r8, r9, r10, r11, r12, r13, r14, r15, r16, r17, r18, r19, r20,
       r21, r22, r23, r24, r25, r26, r27, r28, r29, r30, r31;

  Demultiplexer #(.select(5), .disabled(0)) demultiplexer_1 (
    .out0(_0), .out1(_1), .out2(_2), .out3(_3), .out4(_4), .out5(_5), .out6(_6), .out7(_7), .out8(_8),
    .out9(_9), .out10(_10), .out11(_11), .out12(_12), .out13(_13), .out14(_14), .out15(_15), .out16(_16),
    .out17(_17), .out18(_18), .out19(_19), .out20(_20), .out21(_21), .out22(_22), .out23(_23), .out24(_24),
    .out25(_25), .out26(_26), .out27(_27), .out28(_28), .out29(_29), .out30(_30), .out31(_31), .in(1'b1),
    .sel(y), .en(write));
  _32buffer_el u_32buffer_el_1 (
    .\input (in_1), ._1___buffer_read(_0), .out_5(r0), .video(out_5), ._1___buffer_write___clr(show));
  _32buffer_el u_32buffer_el_2 (
    .\input (in_1), ._1___buffer_read(_1), .out_5(r1), .video(out_6), ._1___buffer_write___clr(show));
  _32buffer_el u_32buffer_el_3 (
    .\input (in_1), ._1___buffer_read(_2), .out_5(r2), .video(out_7), ._1___buffer_write___clr(show));
  _32buffer_el u_32buffer_el_4 (
    .\input (in_1), ._1___buffer_read(_3), .out_5(r3), .video(out_8), ._1___buffer_write___clr(show));
  _32buffer_el u_32buffer_el_5 (
    .\input (in_1), ._1___buffer_read(_4), .out_5(r4), .video(out_9), ._1___buffer_write___clr(show));
  _32buffer_el u_32buffer_el_6 (
    .\input (in_1), ._1___buffer_read(_5), .out_5(r5), .video(out_10), ._1___buffer_write___clr(show));
  _32buffer_el u_32buffer_el_7 (
    .\input (in_1), ._1___buffer_read(_6), .out_5(r6), .video(out_11), ._1___buffer_write___clr(show));
  _32buffer_el u_32buffer_el_8 (
    .\input (in_1), ._1___buffer_read(_7), .out_5(r7), .video(out_12), ._1___buffer_write___clr(show));
  _32buffer_el u_32buffer_el_9 (
    .\input (in_1), ._1___buffer_read(_8), .out_5(r8), .video(out_13), ._1___buffer_write___clr(show));
  _32buffer_el u_32buffer_el_10 (
    .\input (in_1), ._1___buffer_read(_9), .out_5(r9), .video(out_14), ._1___buffer_write___clr(show));
  _32buffer_el u_32buffer_el_11 (
    .\input (in_1), ._1___buffer_read(_10), .out_5(r10), .video(out_15), ._1___buffer_write___clr(show));
  _32buffer_el u_32buffer_el_12 (
    .\input (in_1), ._1___buffer_read(_11), .out_5(r11), .video(out_16), ._1___buffer_write___clr(show));
  _32buffer_el u_32buffer_el_13 (
    .\input (in_1), ._1___buffer_read(_12), .out_5(r12), .video(out_17), ._1___buffer_write___clr(show));
  _32buffer_el u_32buffer_el_14 (
    .\input (in_1), ._1___buffer_read(_13), .out_5(r13), .video(out_18), ._1___buffer_write___clr(show));
  _32buffer_el u_32buffer_el_15 (
    .\input (in_1), ._1___buffer_read(_14), .out_5(r14), .video(out_19), ._1___buffer_write___clr(show));
  _32buffer_el u_32buffer_el_16 (
    .\input (in_1), ._1___buffer_read(_15), .out_5(r15), .video(out_20), ._1___buffer_write___clr(show));
  _32buffer_el u_32buffer_el_17 (
    .\input (in_1), ._1___buffer_read(_16), .out_5(r16), .video(out_21), ._1___buffer_write___clr(show));
  _32buffer_el u_32buffer_el_18 (
    .\input (in_1), ._1___buffer_read(_17), .out_5(r17), .video(out_22), ._1___buffer_write___clr(show));
  _32buffer_el u_32buffer_el_19 (
    .\input (in_1), ._1___buffer_read(_18), .out_5(r18), .video(out_23), ._1___buffer_write___clr(show));
  _32buffer_el u_32buffer_el_20 (
    .\input (in_1), ._1___buffer_read(_19), .out_5(r19), .video(out_24), ._1___buffer_write___clr(show));
  _32buffer_el u_32buffer_el_21 (
    .\input (in_1), ._1___buffer_read(_20), .out_5(r20), .video(out_25), ._1___buffer_write___clr(show));
  _32buffer_el u_32buffer_el_22 (
    .\input (in_1), ._1___buffer_read(_21), .out_5(r21), .video(out_26), ._1___buffer_write___clr(show));
  _32buffer_el u_32buffer_el_23 (
    .\input (in_1), ._1___buffer_read(_22), .out_5(r22), .video(out_27), ._1___buffer_write___clr(show));
  _32buffer_el u_32buffer_el_24 (
    .\input (in_1), ._1___buffer_read(_23), .out_5(r23), .video(out_28), ._1___buffer_write___clr(show));
  _32buffer_el u_32buffer_el_25 (
    .\input (in_1), ._1___buffer_read(_24), .out_5(r24), .video(out_29), ._1___buffer_write___clr(show));
  _32buffer_el u_32buffer_el_26 (
    .\input (in_1), ._1___buffer_read(_25), .out_5(r25), .video(out_30), ._1___buffer_write___clr(show));
  _32buffer_el u_32buffer_el_27 (
    .\input (in_1), ._1___buffer_read(_26), .out_5(r26), .video(out_31), ._1___buffer_write___clr(show));
  _32buffer_el u_32buffer_el_28 (
    .\input (in_1), ._1___buffer_read(_27), .out_5(r27), .video(out_32), ._1___buffer_write___clr(show));
  _32buffer_el u_32buffer_el_29 (
    .\input (in_1), ._1___buffer_read(_28), .out_5(r28), .video(out_33), ._1___buffer_write___clr(show));
  _32buffer_el u_32buffer_el_30 (
    .\input (in_1), ._1___buffer_read(_29), .out_5(r29), .video(out_34), ._1___buffer_write___clr(show));
  _32buffer_el u_32buffer_el_31 (
    .\input (in_1), ._1___buffer_read(_30), .out_5(r30), .video(out_35), ._1___buffer_write___clr(show));
  _32buffer_el u_32buffer_el_32 (
    .\input (in_1), ._1___buffer_read(_31), .out_5(r31), .video(out_36), ._1___buffer_write___clr(show));

  // Other names for the same wires on the sheet: inp[31:0] = in_1; w = show

  // Notes on the sheet:
  //   write: pull=down
endmodule
